// Logisim project RF.circ as structural Verilog: 1 circuit, main circuit Register File
module Register_File (
  input  [31:0] in_1,
  input  in_2,
  input  [4:0] in_3,
  input  [4:0] in_4,
  input  [4:0] in_5,
  input  in_6,
  input  in_7,
  input  in_8,
  output [31:0] Sa,
  output [31:0] Sb,
  output [31:0] SP
);

  wire and_1_out, demultiplexer_1_out0, e2, e3, e4, e5, e6, e7, e8, e9, e10, e11, e12, e13, e14, e15, e16,
       e17, e18, e19, e20, e21, e22, e23, e24, e25, e26, e27, e28, e29, e30, e31, e32;
  wire [31:0] s_e2, s_e3, s_e4, s_e5, s_e6, s_e7, s_e8, s_e9, s_e10, s_e11, s_e12, s_e13, s_e14, s_e15,
       s_e16, s_e17, s_e18, s_e19, s_e20, s_e21, s_e22, s_e23, s_e24, s_e25, s_e26, s_e27, s_e28, s_e29,
       s_e30, s_e31;

  Register #(.width(32)) register_1 (.D(in_1), .en(e5), .Q(s_e5), .clk(in_7), .clr(in_6));
  Register #(.width(32)) register_2 (.D(in_1), .en(e9), .Q(s_e9), .clk(in_7), .clr(in_6));
  Register #(.width(32)) register_3 (.D(in_1), .en(e13), .Q(s_e13), .clk(in_7), .clr(in_6));
  // Probe on s_e2
  Register #(.width(32)) register_4 (.D(in_1), .en(e2), .Q(s_e2), .clk(in_7), .clr(in_6));
  // Probe on s_e5
  Register #(.width(32)) register_5 (.D(in_1), .en(e10), .Q(s_e10), .clk(in_7), .clr(in_6));
  Register #(.width(32)) register_6 (.D(in_1), .en(e14), .Q(s_e14), .clk(in_7), .clr(in_6));
  and and_1 (and_1_out, in_2, in_8);
  // Probe on s_e3
  Register #(.width(32)) register_7 (.D(in_1), .en(e3), .Q(s_e3), .clk(in_7), .clr(in_6));
  Register #(.width(32)) register_8 (.D(in_1), .en(e6), .Q(s_e6), .clk(in_7), .clr(in_6));
  Register #(.width(32)) register_9 (.D(in_1), .en(e11), .Q(s_e11), .clk(in_7), .clr(in_6));
  Register #(.width(32)) register_10 (.D(in_1), .en(e15), .Q(s_e15), .clk(in_7), .clr(in_6));
  // Probe on s_e4
  Register #(.width(32)) register_11 (.D(in_1), .en(e4), .Q(s_e4), .clk(in_7), .clr(in_6));
  Register #(.width(32)) register_12 (.D(in_1), .en(e7), .Q(s_e7), .clk(in_7), .clr(in_6));
  Register #(.width(32)) register_13 (.D(in_1), .en(e12), .Q(s_e12), .clk(in_7), .clr(in_6));
  Register #(.width(32)) register_14 (.D(in_1), .en(e16), .Q(s_e16), .clk(in_7), .clr(in_6));
  Register #(.width(32)) register_15 (.D(in_1), .en(e8), .Q(s_e8), .clk(in_7), .clr(in_6));
  Multiplexer #(.select(5), .width(32), .enable("false")) multiplexer_1 (
    .in0({32{1'b0}}), .in1(s_e2), .in2(s_e3), .in3(s_e4), .in4(s_e5), .in5(s_e6), .in6(s_e7), .in7(s_e8),
    .in8(s_e9), .in9(s_e10), .in10(s_e11), .in11(s_e12), .in12(s_e13), .in13(s_e14), .in14(s_e15),
    .in15(s_e16), .in16(s_e17), .in17(s_e18), .in18(s_e19), .in19(s_e20), .in20(s_e21), .in21(s_e22),
    .in22(s_e23), .in23(s_e24), .in24(s_e25), .in25(s_e26), .in26(s_e27), .in27(s_e28), .in28(s_e29),
    .in29(s_e30), .in30(s_e31), .in31(SP), .out(Sa), .sel(in_3));
  Demultiplexer #(.select(5), .enable("false")) demultiplexer_1 (
    .out0(demultiplexer_1_out0), .out1(e2), .out2(e3), .out3(e4), .out4(e5), .out5(e6), .out6(e7), .out7(e8),
    .out8(e9), .out9(e10), .out10(e11), .out11(e12), .out12(e13), .out13(e14), .out14(e15), .out15(e16),
    .out16(e17), .out17(e18), .out18(e19), .out19(e20), .out20(e21), .out21(e22), .out22(e23), .out23(e24),
    .out24(e25), .out25(e26), .out26(e27), .out27(e28), .out28(e29), .out29(e30), .out30(e31), .out31(e32),
    .in(in_2), .sel(in_4));
  Register #(.width(32)) register_16 (.D(in_1), .en(e17), .Q(s_e17), .clk(in_7), .clr(in_6));
  Register #(.width(32)) register_17 (.D(in_1), .en(e21), .Q(s_e21), .clk(in_7), .clr(in_6));
  Register #(.width(32)) register_18 (.D(in_1), .en(e25), .Q(s_e25), .clk(in_7), .clr(in_6));
  Register #(.width(32)) register_19 (.D(in_1), .en(e29), .Q(s_e29), .clk(in_7), .clr(in_6));
  Register #(.width(32)) register_20 (.D(in_1), .en(e18), .Q(s_e18), .clk(in_7), .clr(in_6));
  Register #(.width(32)) register_21 (.D(in_1), .en(e22), .Q(s_e22), .clk(in_7), .clr(in_6));
  Register #(.width(32)) register_22 (.D(in_1), .en(e26), .Q(s_e26), .clk(in_7), .clr(in_6));
  Register #(.width(32)) register_23 (.D(in_1), .en(e30), .Q(s_e30), .clk(in_7), .clr(in_6));
  Register #(.width(32)) register_24 (.D(in_1), .en(e19), .Q(s_e19), .clk(in_7), .clr(in_6));
  Register #(.width(32)) register_25 (.D(in_1), .en(e23), .Q(s_e23), .clk(in_7), .clr(in_6));
  Register #(.width(32)) register_26 (.D(in_1), .en(e27), .Q(s_e27), .clk(in_7), .clr(in_6));
  Register #(.width(32)) register_27 (.D(in_1), .en(e31), .Q(s_e31), .clk(in_7), .clr(in_6));
  Multiplexer #(.select(5), .width(32), .enable("false")) multiplexer_2 (
    .in0({32{1'b0}}), .in1(s_e2), .in2(s_e3), .in3(s_e4), .in4(s_e5), .in5(s_e6), .in6(s_e7), .in7(s_e8),
    .in8(s_e9), .in9(s_e10), .in10(s_e11), .in11(s_e12), .in12(s_e13), .in13(s_e14), .in14(s_e15),
    .in15(s_e16), .in16(s_e17), .in17(s_e18), .in18(s_e19), .in19(s_e20), .in20(s_e21), .in21(s_e22),
    .in22(s_e23), .in23(s_e24), .in24(s_e25), .in25(s_e26), .in26(s_e27), .in27(s_e28), .in28(s_e29),
    .in29(s_e30), .in30(s_e31), .in31(SP), .out(Sb), .sel(in_5));
  Register #(.width(32)) register_28 (.D(in_1), .en(e20), .Q(s_e20), .clk(in_7), .clr(in_6));
  Register #(.width(32)) register_29 (.D(in_1), .en(e24), .Q(s_e24), .clk(in_7), .clr(in_6));
  Register #(.width(32)) register_30 (.D(in_1), .en(e28), .Q(s_e28), .clk(in_7), .clr(in_6));
  Register #(.width(32)) register_31 (.D(in_1), .en(e32), .Q(SP), .clk(in_7), .clr(in_6));

  // Other names for the same wires on the sheet: EN = in_8; escribir[4:0] = in_4; Input[31:0] = in_1;
  //   leer_a[4:0] = in_3; leer_b[4:0] = in_5; leer_escribir = in_2; reloj = in_7; reset = in_6; s_e32[31:0] = SP

  // Notes on the sheet:
  //   SP
endmodule
