// Logisim project complement_I.circ as structural Verilog: 5 circuits, main circuit beq
module beq (
  input  [31:0] Rt,
  input  [31:0] Rs,
  input  [15:0] in_3,
  output [31:0] OUT
);

  wire comparator_1_eq;

  Comparator #(.width(32)) comparator_1 (.a(Rt), .b(Rs), .eq(comparator_1_eq));  // open: gt, lt
  Multiplexer #(.width(32), .enable("false")) multiplexer_1 (
    .in0({32{1'b0}}), .in1({{15{in_3[15]}}, in_3[14:0], 2'b00}), .out(OUT), .sel(comparator_1_eq));

  // Other names for the same wires on the sheet: out_t[31:2] = {{15{in_3[15]}}, in_3[14:0]}
endmodule

module bne (
  input  [31:0] Rt,
  input  [31:0] Rs,
  input  [15:0] in_3,
  output [31:0] OUT
);

  wire comparator_1_eq;

  Comparator #(.width(32)) comparator_1 (.a(Rt), .b(Rs), .eq(comparator_1_eq));  // open: gt, lt
  Multiplexer #(.width(32)) multiplexer_1 (
    .in0({{15{in_3[15]}}, in_3[14:0], 2'b00}), .in1({32{1'b0}}), .out(OUT), .sel(comparator_1_eq));  // open: en

  // Other names for the same wires on the sheet: out_t[31:2] = {{15{in_3[15]}}, in_3[14:0]}
endmodule

module blez (
  input  [31:0] Rs,
  input  [15:0] in_2,
  output [31:0] OUT
);

  wire comparator_1_eq, comparator_2_lt, or_1_out;

  Comparator #(.width(32)) comparator_1 (.a(Rs), .b({32{1'b0}}), .eq(comparator_1_eq));  // open: gt, lt
  Comparator #(.width(32)) comparator_2 (.a(Rs), .b({32{1'b0}}), .lt(comparator_2_lt));  // open: gt, eq
  or or_1 (or_1_out, comparator_1_eq, comparator_2_lt);
  Multiplexer #(.width(32), .enable("false")) multiplexer_1 (
    .in0({32{1'b0}}), .in1({{15{in_2[15]}}, in_2[14:0], 2'b00}), .out(OUT), .sel(or_1_out));

  // Other names for the same wires on the sheet: out_t[31:2] = {{15{in_2[15]}}, in_2[14:0]}
endmodule

module bgtz (
  input  [31:0] Rs,
  input  [15:0] in_2,
  output [31:0] OUT
);

  wire comparator_1_gt;

  Comparator #(.width(32)) comparator_1 (.a(Rs), .b({32{1'b0}}), .gt(comparator_1_gt));  // open: eq, lt
  Multiplexer #(.width(32), .enable("false")) multiplexer_1 (
    .in0({32{1'b0}}), .in1({{15{in_2[15]}}, in_2[14:0], 2'b00}), .out(OUT), .sel(comparator_1_gt));

  // Other names for the same wires on the sheet: out_t[31:2] = {{15{in_2[15]}}, in_2[14:0]}
endmodule

module bltz (
  input  [31:0] Rs,
  input  [15:0] in_2,
  output [31:0] OUT
);

  wire comparator_1_lt;

  Comparator #(.width(32)) comparator_1 (.a(Rs), .b({32{1'b0}}), .lt(comparator_1_lt));  // open: gt, eq
  Multiplexer #(.width(32), .enable("false")) multiplexer_1 (
    .in0({32{1'b0}}), .in1({{15{in_2[15]}}, in_2[14:0], 2'b00}), .out(OUT), .sel(comparator_1_lt));

  // Other names for the same wires on the sheet: out_t[31:2] = {{15{in_2[15]}}, in_2[14:0]}
endmodule
