// Logisim project instrucciones_miscelanea.circ as structural Verilog: 8 circuits, main circuit andi
module andi (
  input  [31:0] Rs,
  input  [15:0] cons,
  output [31:0] Output
);

  assign Output = Rs & {{16{1'b0}}, cons};  // AND_Gate and_1, 32 bits wide

  // Notes on the sheet:
  //   andi
endmodule

module slt___sltu (
  input  in_1,
  input  [31:0] Rt,
  input  [31:0] Rs,
  output [31:0] Output
);

  wire [31:0] complemento_a_2_simple_1_output, complemento_a_2_simple_2_output, Rs_star, Rt_star;

  Comparator #(.width(32)) comparator_1 (.a(Rt_star), .b(Rs_star), .gt(Output[0]));  // open: eq, lt
  complemento_a_2_simple complemento_a_2_simple_1 (.in_1(Rt), .Output(complemento_a_2_simple_1_output));
  Multiplexer #(.width(32), .enable("false")) multiplexer_1 (
    .in0(Rt), .in1(complemento_a_2_simple_1_output), .out(Rt_star), .sel(in_1));
  Multiplexer #(.width(32), .enable("false")) multiplexer_2 (
    .in0(Rs), .in1(complemento_a_2_simple_2_output), .out(Rs_star), .sel(in_1));
  complemento_a_2_simple complemento_a_2_simple_2 (.in_1(Rs), .Output(complemento_a_2_simple_2_output));

  assign Output[31:1] = {31{1'b0}};

  // Other names for the same wires on the sheet: con_signo = in_1; a = Output[0]

  // Notes on the sheet:
  //   slt / sltu
endmodule

module complemento_a_2_simple (
  input  [31:0] in_1,
  output [31:0] Output
);

  wire [31:0] not_1_out;

  not not_1 (not_1_out[0], in_1[0]);
  not not_2 (not_1_out[1], in_1[1]);
  not not_3 (not_1_out[2], in_1[2]);
  not not_4 (not_1_out[3], in_1[3]);
  not not_5 (not_1_out[4], in_1[4]);
  not not_6 (not_1_out[5], in_1[5]);
  not not_7 (not_1_out[6], in_1[6]);
  not not_8 (not_1_out[7], in_1[7]);
  not not_9 (not_1_out[8], in_1[8]);
  not not_10 (not_1_out[9], in_1[9]);
  not not_11 (not_1_out[10], in_1[10]);
  not not_12 (not_1_out[11], in_1[11]);
  not not_13 (not_1_out[12], in_1[12]);
  not not_14 (not_1_out[13], in_1[13]);
  not not_15 (not_1_out[14], in_1[14]);
  not not_16 (not_1_out[15], in_1[15]);
  not not_17 (not_1_out[16], in_1[16]);
  not not_18 (not_1_out[17], in_1[17]);
  not not_19 (not_1_out[18], in_1[18]);
  not not_20 (not_1_out[19], in_1[19]);
  not not_21 (not_1_out[20], in_1[20]);
  not not_22 (not_1_out[21], in_1[21]);
  not not_23 (not_1_out[22], in_1[22]);
  not not_24 (not_1_out[23], in_1[23]);
  not not_25 (not_1_out[24], in_1[24]);
  not not_26 (not_1_out[25], in_1[25]);
  not not_27 (not_1_out[26], in_1[26]);
  not not_28 (not_1_out[27], in_1[27]);
  not not_29 (not_1_out[28], in_1[28]);
  not not_30 (not_1_out[29], in_1[29]);
  not not_31 (not_1_out[30], in_1[30]);
  not not_32 (not_1_out[31], in_1[31]);
  Adder #(.width(32)) adder_1 (.a(not_1_out), .b(32'h1), .out(Output));  // open: cin, cout
endmodule

module addi (
  input  [31:0] Rs,
  input  [15:0] cons,
  output [31:0] Output
);

  Adder #(.width(32)) adder_1 (.a(Rs), .b({{17{cons[15]}}, cons[14:0]}), .out(Output));  // open: cin, cout

  // Notes on the sheet:
  //   addi
endmodule

module slti___sltiu (
  input  in_1,
  input  [31:0] Rs,
  input  [15:0] \const ,
  output [31:0] Output
);

  wire [31:0] complemento_a_2_simple_1_output, Rs_star;

  complemento_a_2_simple complemento_a_2_simple_1 (.in_1(Rs), .Output(complemento_a_2_simple_1_output));
  Comparator #(.width(32)) comparator_1 (
    .a(Rs_star), .b({{17{\const [15]}}, \const [14:0]}), .lt(Output[0]));  // open: gt, eq
  Multiplexer #(.width(32), .enable("false")) multiplexer_1 (
    .in0(Rs), .in1(complemento_a_2_simple_1_output), .out(Rs_star), .sel(in_1));

  assign Output[31:1] = {31{1'b0}};

  // Other names for the same wires on the sheet: con_signo = in_1; a = Output[0]

  // Notes on the sheet:
  //   slti / sltiu
endmodule

module lw___sw (
  input  in_1,
  input  [31:0] Rs,
  input  [15:0] in_3,
  output [3:0] Mask,
  output [1:0] Mask_2,
  output [15:0] Addres
);

  wire [31:0] adder_1_out;
  wire [31:2] Concatenacion;

  Adder #(.width(32)) adder_1 (.a(Rs), .b({{17{in_3[15]}}, in_3[14:0]}), .out(adder_1_out));  // open: cin, cout
  Multiplexer #(.width(32)) multiplexer_1 (
    .in0(adder_1_out), .out({Concatenacion[31:20], Addres, Concatenacion[3:2], Mask_2}), .sel(1'b0), .en(in_1));  // open: in1
  Decoder #(.select(2)) decoder_1 (
    .out0(Mask[0]), .out1(Mask[1]), .out2(Mask[2]), .out3(Mask[3]), .sel(Concatenacion[3:2]));  // open: en

  // Other names for the same wires on the sheet: Const[15:0] = in_3; Concatenacion (some bits) = {Addres, Mask_2};
  //   EN = in_1
endmodule

module ori (
  input  [31:0] Rs,
  input  [15:0] cons,
  output [31:0] Output
);

  assign Output = Rs | {{16{1'b0}}, cons};  // OR_Gate or_1, 32 bits wide
endmodule

module xori (
  input  [31:0] Rs,
  input  [15:0] cons,
  output [31:0] Output
);

  assign Output = Rs ^ {{16{1'b0}}, cons};  // XOR_Gate xor_1, 32 bits wide
endmodule
