// Logisim project RF.circ as structural Verilog: 10 circuits, main circuit S-MIPS Board
module S_MIPS_Board (
  input  DESHABILITAR_DISPATCHER,
  output halt
);

  wire button_1_out, CLK, CS, d_ff_1_q, LCLR, LoadRAM, LoadRAMOn, LW, R_R_W, R_W, ram_dispatcher_1_finished,
       RCS, Reset_out, RST, TTY_EN;
  wire [2:0] KDB;
  wire [3:0] LMask, Mask, ram_1_read_time, ram_1_write_time, RMask;
  wire [6:0] KDB_DATA, TTY_DATA;
  wire [15:0] Addr, LAddr, RAddr;
  wire [31:0] I0, I1, I2, I3, LData, ram_1_data_out_0, ram_1_data_out_1, ram_1_data_out_2, ram_1_data_out_3,
       RI0, RI1, RI2, RI3;

  TTY #(.rows(25), .cols(80)) tty_1 (.data(TTY_DATA), .clk(CLK), .we(TTY_EN), .clr(RST));
  not not_1 (LoadRAMOn, ram_dispatcher_1_finished);
  RAM_Dispatcher ram_dispatcher_1 (
    .WriteTime(ram_1_write_time), .Clock(CLK), .Data(LData), .Address(LAddr), .Mask(LMask),
    .Finished(ram_dispatcher_1_finished), .Write(LW), .CLR(LCLR));
  Keyboard #(.buflen(64)) keyboard_1 (.clk(CLK), .re(KDB[0]), .avail(KDB[2]), .data(KDB_DATA));  // open: clr
  RAM ram_1 (
    .Address(RAddr), .Data_Out_0(ram_1_data_out_0), .Data_Out_1(ram_1_data_out_1),
    .Data_Out_2(ram_1_data_out_2), .Data_Out_3(ram_1_data_out_3), .Data_In_0(RI0), .Data_In_1(RI1),
    .Data_In_2(RI2), .Data_In_3(RI3), .Mask(RMask), .nRead_Write(R_R_W), .Chip_Select(RCS),
    .Read_Time(ram_1_read_time), .Reset(button_1_out), .Write_Time(ram_1_write_time));
  Button button_1 (.out(button_1_out));
  D_Flip_Flop d_ff_1 (.clk(CLK), .D(1'b1), .Q(d_ff_1_q), .reset(Reset_out));  // open: Qn, preset, en
  Button Reset (.out(Reset_out));
  S_MIPS s_mips_1 (
    .Kbd_Enable(KDB[0]), .Address(Addr), .Kbd_Clear(KDB[1]), .Kbd_Available(KDB[2]), .RAM_In_0(I0),
    .Kbd_ASCII_Data(KDB_DATA), .RAM_In_1(I1), .TTY_Enable(TTY_EN), .RAM_In_2(I2), .RAM_In_3(I2),
    .TTY_ASCII_Data(TTY_DATA), .Reset(RST), .RAM_Out_0(ram_1_data_out_0), .Clock(CLK),
    .RAM_Out_1(ram_1_data_out_1), .Stop(halt), .RAM_Out_2(ram_1_data_out_2), .RAM_Out_3(ram_1_data_out_3),
    .Mask(Mask), .Read_Time(ram_1_read_time), .Write_Time(ram_1_write_time), .nRead_Write(R_W),
    .Chip_Select(CS));
  D_Flip_Flop d_ff_2 (.clk(CLK), .D(d_ff_1_q), .Qn(LCLR), .reset(Reset_out));  // open: Q, preset, en
  or or_1 (RST, LCLR, LoadRAM);
  Clock clock_1 (.out(CLK));
  Multiplexer #(.width(32), .enable("false")) multiplexer_1 (.in0(I0), .in1(LData), .out(RI0), .sel(LoadRAM));
  Multiplexer #(.width(32), .enable("false")) multiplexer_2 (.in0(I1), .in1(LData), .out(RI1), .sel(LoadRAM));
  Multiplexer #(.width(32), .enable("false")) multiplexer_3 (.in0(I2), .in1(LData), .out(RI2), .sel(LoadRAM));
  Multiplexer #(.width(32), .enable("false")) multiplexer_4 (.in0(I3), .in1(LData), .out(RI3), .sel(LoadRAM));
  and and_1 (LoadRAM, ~DESHABILITAR_DISPATCHER, LoadRAMOn);  // AND_Gate
  Multiplexer #(.width(16), .enable("false")) multiplexer_5 (.in0(Addr), .in1(LAddr), .out(RAddr), .sel(LoadRAM));
  Multiplexer #(.width(4), .enable("false")) multiplexer_6 (.in0(Mask), .in1(LMask), .out(RMask), .sel(LoadRAM));
  Multiplexer #(.enable("false")) multiplexer_7 (.in0(CS), .in1(LW), .out(RCS), .sel(LoadRAM));
  Multiplexer #(.enable("false")) multiplexer_8 (.in0(R_W), .in1(LW), .out(R_R_W), .sel(LoadRAM));

  // Notes on the sheet:
  //   NO MODIFICAR
  //   Keyboard
endmodule

module RAM (
  input  [15:0] Address,
  input  [31:0] Data_In_0,
  input  [31:0] Data_In_1,
  input  [31:0] Data_In_2,
  input  [31:0] Data_In_3,
  input  [3:0] Mask,
  input  nRead_Write,
  input  Chip_Select,
  input  Reset,
  output [31:0] Data_Out_0,
  output [31:0] Data_Out_1,
  output [31:0] Data_Out_2,
  output [31:0] Data_Out_3,
  output [3:0] Read_Time,
  output [3:0] Write_Time
);

  wire and_2_out, and_3_out, and_4_out, and_5_out, and_6_out, and_7_out, and_8_out, and_9_out, Changed, CLK,
       comparator_2_eq, comparator_3_eq, comparator_4_eq, comparator_5_eq, comparator_6_eq, Count,
       demultiplexer_3_out0, Idle, Idle_q, Load, Load0, Load1, nand_1_out, or_1_out, or_2_out, or_3_out,
       or_4_out, or_5_out, or_6_out, or_7_out, or_8_out, or_9_out, or_10_out, Proc_q, Update_Mem, Zero_Time;
  wire [3:0] counter_1_q, multiplexer_1_out, subtractor_1_out;
  wire [31:0] register_1_q, register_2_q, register_3_q, register_4_q, register_5_q;

  // Probe on 4'b0011
  // Probe on 4'b0010
  Multiplexer #(.width(4), .enable("false")) multiplexer_1 (
    .in0(4'b0011), .in1(4'b0010), .out(multiplexer_1_out), .sel(nRead_Write));
  or or_1 (or_1_out, Idle, Update_Mem);
  or or_2 (or_2_out, ~Chip_Select, Reset);  // OR_Gate
  Subtractor #(.width(4)) subtractor_1 (.a(multiplexer_1_out), .b(4'b0010), .out(subtractor_1_out));  // open: bin, bout
  D_Flip_Flop u_Idle (.clk(CLK), .D(or_1_out), .Q(Idle_q), .preset(or_2_out));  // open: Qn, en, reset
  Demultiplexer #(.enable("false")) demultiplexer_1 (.out0(Idle), .out1(Load0), .in(Idle_q), .sel(Changed));
  // Probe on counter_1_q
  Counter #(.width(4), .max('hf)) counter_1 (
    .load(Load), .D(subtractor_1_out), .count(Count), .Q(counter_1_q), .clk(CLK), .clr(or_3_out));  // open: carry
  or or_3 (or_3_out, ~Chip_Select, Reset);  // OR_Gate
  Comparator #(.width(4), .mode("unsigned")) comparator_1 (
    .a(4'b0000), .b(counter_1_q), .eq(Zero_Time));  // open: gt, lt
  or or_4 (or_4_out, Count, Load0, Load1);
  Register #(.width(32)) register_1 (.D(Data_In_0), .en(Chip_Select), .Q(register_1_q), .clk(CLK), .clr(or_5_out));
  or or_5 (or_5_out, ~Chip_Select, Reset);  // OR_Gate
  Register #(.width(32)) register_2 (.D(Data_In_1), .en(Chip_Select), .Q(register_2_q), .clk(CLK), .clr(or_6_out));
  or or_6 (or_6_out, ~Chip_Select, Reset);  // OR_Gate
  Register #(.width(32)) register_3 (.D(Data_In_2), .en(Chip_Select), .Q(register_3_q), .clk(CLK), .clr(or_7_out));
  or or_7 (or_7_out, ~Chip_Select, Reset);  // OR_Gate
  Register #(.width(32)) register_4 (.D(Data_In_3), .en(Chip_Select), .Q(register_4_q), .clk(CLK), .clr(or_8_out));
  or or_8 (or_8_out, ~Chip_Select, Reset);  // OR_Gate
  Register #(.width(32)) register_5 (
    .D({{11{1'b1}}, nRead_Write, Mask, Address}), .en(Chip_Select), .Q(register_5_q), .clk(CLK),
    .clr(or_9_out));
  or or_9 (or_9_out, ~Chip_Select, Reset);  // OR_Gate
  D_Flip_Flop Proc (.clk(CLK), .D(or_4_out), .Q(Proc_q), .reset(or_10_out));  // open: Qn, preset, en
  or or_10 (or_10_out, ~Chip_Select, Reset);  // OR_Gate
  Demultiplexer #(.enable("false")) demultiplexer_2 (
    .out0(Count), .out1(Update_Mem), .in(demultiplexer_3_out0), .sel(Zero_Time));
  Demultiplexer #(.enable("false")) demultiplexer_3 (
    .out0(demultiplexer_3_out0), .out1(Load1), .in(Proc_q), .sel(Changed));
  Clock clock_1 (.out(CLK));
  Comparator #(.width(32)) comparator_2 (.a(register_1_q), .b(Data_In_0), .eq(comparator_2_eq));  // open: gt, lt
  Comparator #(.width(32)) comparator_3 (.a(register_2_q), .b(Data_In_1), .eq(comparator_3_eq));  // open: gt, lt
  Comparator #(.width(32)) comparator_4 (.a(register_3_q), .b(Data_In_2), .eq(comparator_4_eq));  // open: gt, lt
  Comparator #(.width(32)) comparator_5 (.a(register_4_q), .b(Data_In_3), .eq(comparator_5_eq));  // open: gt, lt
  Comparator #(.width(32)) comparator_6 (
    .a(register_5_q), .b({{11{1'b1}}, nRead_Write, Mask, Address}), .eq(comparator_6_eq));  // open: gt, lt
  nand nand_1 (nand_1_out, comparator_6_eq, comparator_2_eq, comparator_3_eq, comparator_4_eq, comparator_5_eq);
  and and_1 (Changed, nand_1_out, Chip_Select);
  or or_11 (Load, Count, Load1, Load0);
  and and_2 (and_2_out, Mask[0], Update_Mem, nRead_Write);
  and and_3 (and_3_out, Mask[1], Update_Mem, nRead_Write);
  and and_4 (and_4_out, Mask[2], Update_Mem, nRead_Write);
  and and_5 (and_5_out, Mask[3], Update_Mem, nRead_Write);
  RAM_part #(.addrWidth(16), .dataWidth(32), .bus("separate")) ram_1 (
    .addr(Address), .din(Data_In_0), .data(Data_Out_0), .str(and_2_out), .sel(Chip_Select), .clk(CLK),
    .ld(and_6_out), .clr(Reset));
  and and_6 (and_6_out, ~nRead_Write, Idle);  // AND_Gate
  RAM_part #(.addrWidth(16), .dataWidth(32), .bus("separate")) ram_2 (
    .addr(Address), .din(Data_In_1), .data(Data_Out_1), .str(and_3_out), .sel(Chip_Select), .clk(CLK),
    .ld(and_7_out), .clr(Reset));
  and and_7 (and_7_out, ~nRead_Write, Idle);  // AND_Gate
  RAM_part #(.addrWidth(16), .dataWidth(32), .bus("separate")) ram_3 (
    .addr(Address), .din(Data_In_2), .data(Data_Out_2), .str(and_4_out), .sel(Chip_Select), .clk(CLK),
    .ld(and_8_out), .clr(Reset));
  and and_8 (and_8_out, ~nRead_Write, Idle);  // AND_Gate
  RAM_part #(.addrWidth(16), .dataWidth(32), .bus("separate")) ram_4 (
    .addr(Address), .din(Data_In_3), .data(Data_Out_3), .str(and_5_out), .sel(Chip_Select), .clk(CLK),
    .ld(and_9_out), .clr(Reset));
  and and_9 (and_9_out, ~nRead_Write, Idle);  // AND_Gate

  assign Read_Time = 4'b0011;
  assign Write_Time = 4'b0010;

  // Other names for the same wires on the sheet: M0 = Mask[0]; M1 = Mask[1]; M2 = Mask[2]; M3 = Mask[3];
  //   RW = nRead_Write; CLR = Reset; CS = Chip_Select; Load2 = Count

  // Notes on the sheet:
  //   NO MODIFICAR
  //   excepto quizás los valores RT y WT
  //   BANK0
  //   BANK1
  //   BANK2
  //   BANK3
endmodule

module S_MIPS (
  input  Kbd_Available,
  input  [6:0] Kbd_ASCII_Data,
  input  [31:0] RAM_Out_0,
  input  [31:0] RAM_Out_1,
  input  Reset,
  input  [31:0] RAM_Out_2,
  input  Clock,
  input  [31:0] RAM_Out_3,
  input  [3:0] Read_Time,
  input  [3:0] Write_Time,
  output Kbd_Enable,
  output [15:0] Address,
  output Kbd_Clear,
  output TTY_Enable,
  output [6:0] TTY_ASCII_Data,
  output Stop,
  output [31:0] RAM_In_0,
  output [31:0] RAM_In_1,
  output [31:0] RAM_In_2,
  output [31:0] RAM_In_3,
  output [3:0] Mask,
  output nRead_Write,
  output Chip_Select
);


  // Other names for the same wires on the sheet: CLK = Clock; CLR = Reset; CS = Chip_Select;
  //   KBD_AVAIL = Kbd_Available; KBD_CLR = Kbd_Clear; KBD_DATA[6:0] = Kbd_ASCII_Data; RAM_A[15:0] = Address;
  //   RAM_INPUT_0[31:0] = RAM_In_0; RAM_INPUT_1[31:0] = RAM_In_1; RAM_INPUT_2[31:0] = RAM_In_2;
  //   RAM_INPUT_3[31:0] = RAM_In_3; RAM_MASK[3:0] = Mask; RAM_OUTPUT_0[31:0] = RAM_Out_0;
  //   RAM_OUTPUT_1[31:0] = RAM_Out_1; RAM_OUTPUT_2[31:0] = RAM_Out_2; RAM_OUTPUT_3[31:0] = RAM_Out_3;
  //   RW = nRead_Write; TTY_DATA[6:0] = TTY_ASCII_Data

  // Notes on the sheet:
  //   RAM ADDRESS
  //   DATA FROM RAM
  //   DATA TO RAM
  //   DATA WRITE MASK
  //   RAM TIMING
  //   RAM CONTROL
  //   KEYBOARD
  //   TTY
  //   SEQUENCING
endmodule

module RAM_Dispatcher (
  input  [3:0] WriteTime,
  input  Clock,
  input  CLR,
  output [31:0] Data,
  output [15:0] Address,
  output [3:0] Mask,
  output Finished,
  output Write
);

  wire demultiplexer_2_out1, demultiplexer_3_out1, End, IDLE_q, IncAddr, Load, or_1_out, or_2_out, While_q,
       WriteEnd;
  wire [3:0] counter_1_q;
  wire [31:0] CurrentAddress_q;

  Counter #(.width(32), .max('hffffffff)) CurrentAddress (
    .count(IncAddr), .Q({CurrentAddress_q[31:18], Address, CurrentAddress_q[1:0]}), .clk(Clock), .clr(CLR));  // open: load, D, carry
  or or_1 (or_1_out, IncAddr, demultiplexer_3_out1, Finished);
  D_Flip_Flop IDLE (.clk(Clock), .D(or_1_out), .Q(IDLE_q), .preset(CLR));  // open: Qn, en, reset
  Demultiplexer #(.enable("false")) demultiplexer_1 (.out0(Load), .out1(Finished), .in(IDLE_q), .sel(End));
  D_Flip_Flop While (.clk(Clock), .D(or_2_out), .Q(While_q), .reset(CLR));  // open: Qn, preset, en
  or or_2 (or_2_out, Write, Load);
  RAM_part #(.addrWidth(18), .dataWidth(32)) ram_1 (
    .addr({Address, CurrentAddress_q[1:0]}), .data(Data), .clk(Clock));  // open: sel, ld, clr
  Demultiplexer #(.enable("false")) demultiplexer_2 (
    .out0(Write), .out1(demultiplexer_2_out1), .in(While_q), .sel(WriteEnd));
  Decoder #(.select(2)) decoder_1 (
    .out0(Mask[0]), .out1(Mask[1]), .out2(Mask[2]), .out3(Mask[3]), .sel(CurrentAddress_q[1:0]));  // open: en
  Demultiplexer #(.enable("false")) demultiplexer_3 (
    .out0(IncAddr), .out1(demultiplexer_3_out1), .in(demultiplexer_2_out1), .sel(End));
  Counter #(.width(4), .max('hf)) counter_1 (
    .load(Load), .D(WriteTime), .count(Write), .Q(counter_1_q), .clk(Clock));  // open: carry, clr
  Comparator #(.width(32)) comparator_1 (.a(Data), .b({32{1'b1}}), .eq(End));  // open: gt, lt
  Comparator #(.width(4)) comparator_2 (.a(4'b0000), .b(counter_1_q), .eq(WriteEnd));  // open: gt, lt

  // Other names for the same wires on the sheet: CLK = Clock; Count = Write; WT[3:0] = WriteTime
endmodule

module Branch_Control_Unit (
  input  [31:0] in_1
);

  wire add, \and , div, divu, I, IE, J, mult, mulu, nop, \nor , \or , P, R, slt, sltu, sub, \xor ;

  Comparator #(.width(6)) comparator_1 (.a(in_1[5:0]), .b({6{1'b0}}), .eq(R));  // open: gt, lt
  Comparator #(.width(6)) comparator_2 (.a(in_1[5:0]), .b(6'b001000), .eq(J));  // open: gt, lt
  Comparator #(.width(6)) comparator_3 (.a(in_1[5:0]), .b(6'b011000), .eq(P));  // open: gt, lt
  Comparator #(.width(6)) comparator_4 (.a(in_1[5:0]), .b(6'b000111), .eq(IE));  // open: gt, lt
  nor nor_1 (I, R, J, P, IE);
  Comparator #(.width(6)) comparator_5 (.a(in_1[31:26]), .b({6{1'b0}}), .eq(nop));  // open: gt, lt
  Comparator #(.width(6)) comparator_6 (.a(in_1[31:26]), .b(6'b100000), .eq(add));  // open: gt, lt
  Comparator #(.width(6)) comparator_7 (.a(in_1[31:26]), .b(6'b101010), .eq(sub));  // open: gt, lt
  Comparator #(.width(6)) comparator_8 (.a(in_1[31:26]), .b({6{1'b0}}), .eq(mult));  // open: gt, lt
  Comparator #(.width(6)) comparator_9 (.a(in_1[31:26]), .b(6'b000001), .eq(mulu));  // open: gt, lt
  Comparator #(.width(6)) comparator_10 (.a(in_1[31:26]), .b(6'b001000), .eq(div));  // open: gt, lt
  Comparator #(.width(6)) comparator_11 (.a(in_1[31:26]), .b(6'b001001), .eq(divu));  // open: gt, lt
  Comparator #(.width(6)) comparator_12 (.a(in_1[31:26]), .b(6'b010010), .eq(slt));  // open: gt, lt
  Comparator #(.width(6)) comparator_13 (.a(in_1[31:26]), .b(6'b001000), .eq(\xor ));  // open: gt, lt
  Comparator #(.width(6)) comparator_14 (.a(in_1[31:26]), .b(6'b010011), .eq(sltu));  // open: gt, lt
  Comparator #(.width(6)) comparator_15 (.a(in_1[31:26]), .b(6'b000100), .eq(\and ));  // open: gt, lt
  Comparator #(.width(6)) comparator_16 (.a(in_1[31:26]), .b(6'b000101), .eq(\or ));  // open: gt, lt
  Comparator #(.width(6)) comparator_17 (.a(in_1[31:26]), .b(6'b001111), .eq(\nor ));  // open: gt, lt

  // Other names for the same wires on the sheet: _6_fisrt_input_bits[5:0] = in_1[5:0]; Input[31:0] = in_1;
  //   _6_last_bists_input[5:0] = in_1[31:26]
endmodule

module Instruction_Decoder (
  input  [31:0] in_1,
  output [5:0] Op_Code,
  output [4:0] Rt,
  output [15:0] Constante,
  output [5:0] Func_Code,
  output [4:0] Rd,
  output [4:0] Rs,
  output [4:0] x,
  output [25:0] Destino_salto
);


  assign Constante = in_1[31:16];
  assign Destino_salto = in_1[31:6];
  assign Func_Code = in_1[31:26];
  assign Op_Code = in_1[5:0];
  assign Rd = in_1[20:16];
  assign Rs = in_1[10:6];
  assign Rt = in_1[15:11];
  assign x = in_1[20:16];

  // Other names for the same wires on the sheet: Input[31:0] = in_1

  // Notes on the sheet:
  //   Instruction Decoder
endmodule

module ALU (
  input  [5:0] in_1,
  input  [31:0] in_2,
  input  [31:0] in_3,
  input  [15:0] in_4
);

  wire con_signo;
  wire [31:0] add, \and , div___divu_hi, div__divu_lo, mul, mult___mulu_hi, mult___mulu_lo, \nor , \or , sub,
       \xor ;

  Adder #(.width(32)) adder_1 (.a(in_2), .b(in_3), .out(add));  // open: cin, cout
  Subtractor #(.width(32)) subtractor_1 (.a(in_2), .b(in_3), .out(sub));  // open: bin, bout
  assign \and  = in_2 & in_3;  // AND_Gate and_1, 32 bits wide
  assign \or  = in_2 | in_3;  // OR_Gate or_1, 32 bits wide
  assign \xor  = in_2 ^ in_3;  // XOR_Gate xor_1, 32 bits wide
  assign \nor  = ~(in_2 | in_3);  // NOR_Gate nor_1, 32 bits wide
  div___divu div_divu_1 (.in_1(in_2), .in_2(in_3), .in_3(con_signo), .Hi(div__divu_lo), .Lo(div___divu_hi));
  mult___mulu mult_mulu_1 (.in_1(in_2), .in_2(in_3), .in_3(con_signo), .hi(mult___mulu_hi), .lo(mult___mulu_lo));
  Multiplier #(.width(32)) multiplier_1 (.a(in_2), .b(in_3), .out(mul));  // open: cin, cout

  // Other names for the same wires on the sheet: Const[15:0] = in_4; Operacion[5:0] = in_1; Rs[31:0] = in_2;
  //   Rt[31:0] = in_3
endmodule

module div___divu (
  input  [31:0] in_1,
  input  [31:0] in_2,
  input  in_3,
  output [31:0] Lo,
  output [31:0] Hi
);

  wire [31:0] div_a_negativo, div_b_negativo, div_negativos, div_positivos, divider_2_out, divider_3_out,
       Hi_sin_sg, Lo_sin_sg, minus_a, minus_b, resto_a_negativo, resto_b_negativo, resto_negativo,
       resto_positivo;

  Divider #(.width(32)) divider_1 (.a(in_1), .b(in_2), .out(div_positivos), .rem(resto_positivo));  // open: upper
  Divider #(.width(32)) divider_2 (.a(minus_a), .b(in_2), .out(divider_2_out), .rem(resto_a_negativo));  // open: upper
  Negator #(.width(32)) negator_1 (.in(divider_2_out), .out(div_a_negativo));
  Divider #(.width(32)) divider_3 (.a(in_1), .b(minus_b), .out(divider_3_out), .rem(resto_b_negativo));  // open: upper
  Negator #(.width(32)) negator_2 (.in(divider_3_out), .out(div_b_negativo));
  Divider #(.width(32)) divider_4 (.a(minus_a), .b(minus_b), .out(div_negativos), .rem(resto_negativo));  // open: upper
  // Probe on in_1
  Negator #(.width(32)) negator_3 (.in(in_1), .out(minus_a));
  // Probe on in_2
  Negator #(.width(32)) negator_4 (.in(in_2), .out(minus_b));
  // Probe on Lo
  Multiplexer #(.select(2), .width(32)) multiplexer_1 (
    .in0(div_positivos), .in1(div_a_negativo), .in2(div_b_negativo), .in3(div_negativos), .out(Lo_sin_sg),
    .sel({in_2[31], in_1[31]}));  // open: en
  Multiplexer #(.select(2), .width(32)) multiplexer_2 (
    .in0(resto_positivo), .in1(resto_a_negativo), .in2(resto_b_negativo), .in3(resto_negativo),
    .out(Hi_sin_sg), .sel({in_2[31], in_1[31]}));  // open: en
  // Probe on Hi
  Multiplexer #(.width(32), .enable("false")) multiplexer_3 (
    .in0(div_positivos), .in1(Lo_sin_sg), .out(Lo), .sel(in_3));
  Multiplexer #(.width(32), .enable("false")) multiplexer_4 (
    .in0(resto_positivo), .in1(Hi_sin_sg), .out(Hi), .sel(in_3));

  // Other names for the same wires on the sheet: a[31:0] = in_1; b[31:0] = in_2; con_sig = in_3; a_sig = in_1[31];
  //   selector[1:0] = {in_2[31], in_1[31]}; b_sg = in_2[31]

  // Notes on the sheet:
  //   0 : sin signo
  //   1 : con signo
endmodule

module mult___mulu (
  input  [31:0] in_1,
  input  [31:0] in_2,
  input  in_3,
  output [31:0] hi,
  output [31:0] lo
);

  wire [31:0] minus_a, minus_b, mult_hi, mult_lo, multiplexer_1_out, multiplexer_2_out, mulu_Hi, mulu_Lo,
       negator_1_out, negator_2_out;

  Multiplier #(.width(32)) multiplier_1 (.a(in_1), .b(in_2), .out(mult_lo), .cout(mult_hi));  // open: cin
  Negator #(.width(32)) negator_1 (.in(in_1), .out(negator_1_out));
  Negator #(.width(32)) negator_2 (.in(in_2), .out(negator_2_out));
  // Probe on in_1
  // Probe on multiplexer_1_out
  Multiplexer #(.width(32), .enable("false")) multiplexer_1 (
    .in0(in_1), .in1(negator_1_out), .out(multiplexer_1_out), .sel(in_1[31]));
  Multiplexer #(.width(32), .enable("false")) multiplexer_2 (
    .in0(in_2), .in1(negator_2_out), .out(multiplexer_2_out), .sel(in_2[31]));
  Negator #(.width(32)) negator_3 (.in(in_1), .out(minus_a));
  Multiplier #(.width(32)) multiplier_2 (
    .a(multiplexer_1_out), .b(multiplexer_2_out), .out(mulu_Lo), .cout(mulu_Hi));  // open: cin
  // Probe on multiplexer_2_out
  // Probe on in_2
  Negator #(.width(32)) negator_4 (.in(in_2), .out(minus_b));
  // Probe on lo
  // Probe on hi
  Multiplexer #(.width(32), .enable("false")) multiplexer_3 (.in0(mult_hi), .in1(mulu_Hi), .out(hi), .sel(in_3));
  Multiplexer #(.width(32), .enable("false")) multiplexer_4 (.in0(mult_lo), .in1(mulu_Lo), .out(lo), .sel(in_3));

  // Other names for the same wires on the sheet: a[31:0] = in_1; a_sig = in_1[31]; b[31:0] = in_2; b_sg = in_2[31];
  //   con_sig = in_3

  // Notes on the sheet:
  //   0 : sin signo
  //   1 : con signo
endmodule

module Register_File (
  input  [31:0] in_1,
  input  in_2,
  input  [4:0] in_3,
  input  [4:0] in_4,
  input  [4:0] in_5,
  input  in_6,
  input  in_7,
  output [31:0] Sa,
  output [31:0] Sb
);

  wire e2, e3, e4, e5, e6, e7, e8, e9, e11, e12, e13, e14, e15, e16, e17, e18, e19, e20, e21, e22, e23, e24,
       e25, e26, e27, e28, e29, e30, e31, e32;
  wire [31:0] s_e2, s_e3, s_e4, s_e5, s_e6, s_e7, s_e8, s_e9, s_e10, s_e11, s_e12, s_e13, s_e14, s_e15,
       s_e16, s_e17, s_e18, s_e19, s_e20, s_e21, s_e22, s_e23, s_e24, s_e25, s_e26, s_e27, s_e28, s_e29,
       s_e30, s_e31, s_e32;

  Register #(.width(32)) register_1 (.D(in_1), .en(e5), .Q(s_e5), .clk(in_7), .clr(in_6));
  Register #(.width(32)) register_2 (.D(in_1), .en(e9), .Q(s_e9), .clk(in_7), .clr(in_6));
  Register #(.width(32)) register_3 (.D(in_1), .en(e13), .Q(s_e13), .clk(in_7), .clr(in_6));
  Register #(.width(32)) register_4 (.D(in_1), .en(e2), .Q(s_e2), .clk(in_7), .clr(in_6));
  Register #(.width(32)) register_5 (.D(in_1), .en(e6), .Q(s_e6), .clk(in_7), .clr(in_6));
  Register #(.width(32)) register_6 (.D(in_1), .en(in_7), .Q(s_e10), .clk(in_7), .clr(in_6));
  Register #(.width(32)) register_7 (.D(in_1), .en(e14), .Q(s_e14), .clk(in_7), .clr(in_6));
  Register #(.width(32)) register_8 (.D(in_1), .en(e3), .Q(s_e3), .clk(in_7), .clr(in_6));
  Register #(.width(32)) register_9 (.D(in_1), .en(e7), .Q(s_e7), .clk(in_7), .clr(in_6));
  Register #(.width(32)) register_10 (.D(in_1), .en(e11), .Q(s_e11), .clk(in_7), .clr(in_6));
  Register #(.width(32)) register_11 (.D(in_1), .en(e15), .Q(s_e15), .clk(in_7), .clr(in_6));
  Decoder #(.select(5)) decoder_1 (
    .out1(e2), .out2(e3), .out3(e4), .out4(e5), .out5(e6), .out6(e7), .out7(e8), .out8(e9), .out9(in_7),
    .out10(e11), .out11(e12), .out12(e13), .out13(e14), .out14(e15), .out15(e16), .out16(e17), .out17(e18),
    .out18(e19), .out19(e20), .out20(e21), .out21(e22), .out22(e23), .out23(e24), .out24(e25), .out25(e26),
    .out26(e27), .out27(e28), .out28(e29), .out29(e30), .out30(e31), .out31(e32), .sel(in_4), .en(in_2));  // open: out0
  Register #(.width(32)) register_12 (.D(in_1), .en(e4), .Q(s_e4), .clk(in_7), .clr(in_6));
  Register #(.width(32)) register_13 (.D(in_1), .en(e8), .Q(s_e8), .clk(in_7), .clr(in_6));
  Register #(.width(32)) register_14 (.D(in_1), .en(e12), .Q(s_e12), .clk(in_7), .clr(in_6));
  Register #(.width(32)) register_15 (.D(in_1), .en(e16), .Q(s_e16), .clk(in_7), .clr(in_6));
  Register #(.width(32)) register_16 (.D(in_1), .en(e17), .Q(s_e17), .clk(in_7), .clr(in_6));
  Register #(.width(32)) register_17 (.D(in_1), .en(e21), .Q(s_e21), .clk(in_7), .clr(in_6));
  Register #(.width(32)) register_18 (.D(in_1), .en(e25), .Q(s_e25), .clk(in_7), .clr(in_6));
  Register #(.width(32)) register_19 (.D(in_1), .en(e29), .Q(s_e29), .clk(in_7), .clr(in_6));
  Multiplexer #(.select(5), .width(32)) multiplexer_1 (
    .in0({32{1'b0}}), .in1(s_e2), .in2(s_e3), .in3(s_e4), .in4(s_e5), .in5(s_e6), .in6(s_e7), .in7(s_e8),
    .in8(s_e9), .in9(s_e10), .in10(s_e11), .in11(s_e12), .in12(s_e13), .in13(s_e14), .in14(s_e15),
    .in15(s_e16), .in16(s_e17), .in17(s_e18), .in18(s_e19), .in19(s_e20), .in20(s_e21), .in21(s_e22),
    .in22(s_e23), .in23(s_e24), .in24(s_e25), .in25(s_e26), .in26(s_e27), .in27(s_e28), .in28(s_e29),
    .in29(s_e30), .in30(s_e31), .in31(s_e32), .out(Sa), .sel(in_3));  // open: en
  Register #(.width(32)) register_20 (.D(in_1), .en(e18), .Q(s_e18), .clk(in_7), .clr(in_6));
  Register #(.width(32)) register_21 (.D(in_1), .en(e22), .Q(s_e22), .clk(in_7), .clr(in_6));
  Register #(.width(32)) register_22 (.D(in_1), .en(e26), .Q(s_e26), .clk(in_7), .clr(in_6));
  Register #(.width(32)) register_23 (.D(in_1), .en(e30), .Q(s_e30), .clk(in_7), .clr(in_6));
  Register #(.width(32)) register_24 (.D(in_1), .en(e19), .Q(s_e19), .clk(in_7), .clr(in_6));
  Register #(.width(32)) register_25 (.D(in_1), .en(e23), .Q(s_e23), .clk(in_7), .clr(in_6));
  Register #(.width(32)) register_26 (.D(in_1), .en(e27), .Q(s_e27), .clk(in_7), .clr(in_6));
  Register #(.width(32)) register_27 (.D(in_1), .en(e31), .Q(s_e31), .clk(in_7), .clr(in_6));
  Register #(.width(32)) register_28 (.D(in_1), .en(e20), .Q(s_e20), .clk(in_7), .clr(in_6));
  Register #(.width(32)) register_29 (.D(in_1), .en(e24), .Q(s_e24), .clk(in_7), .clr(in_6));
  Register #(.width(32)) register_30 (.D(in_1), .en(e28), .Q(s_e28), .clk(in_7), .clr(in_6));
  Register #(.width(32)) register_31 (.D(in_1), .en(e32), .Q(s_e32), .clk(in_7), .clr(in_6));
  Multiplexer #(.select(5), .width(32)) multiplexer_2 (
    .in0({32{1'b0}}), .in1(s_e2), .in2(s_e3), .in3(s_e4), .in4(s_e5), .in5(s_e6), .in6(s_e7), .in7(s_e8),
    .in8(s_e9), .in9(s_e10), .in10(s_e11), .in11(s_e12), .in12(s_e13), .in13(s_e14), .in14(s_e15),
    .in15(s_e16), .in16(s_e17), .in17(s_e18), .in18(s_e19), .in19(s_e20), .in20(s_e21), .in21(s_e22),
    .in22(s_e23), .in23(s_e24), .in24(s_e25), .in25(s_e26), .in26(s_e27), .in27(s_e28), .in28(s_e29),
    .in29(s_e30), .in30(s_e31), .in31(s_e32), .out(Sb), .sel(in_5));  // open: en

  // Other names for the same wires on the sheet: escribir[4:0] = in_4; Input[31:0] = in_1; leer_a[4:0] = in_3;
  //   leer_b[4:0] = in_5; leer_escribir = in_2; e10 = in_7; reloj = in_7; reset = in_6
endmodule
