// Logisim project s-mips.circ as structural Verilog: 20 circuits, main circuit S-MIPS Board
module S_MIPS_Board (
  input  DESHABILITAR_DISPATCHER,
  output halt
);

  wire button_1_out, CLK, CS, d_ff_1_q, LCLR, LoadRAM, LoadRAMOn, LW, R_R_W, R_W, ram_dispatcher_1_finished,
       RCS, Reset_out, RST, TTY_EN;
  wire [2:0] KDB;
  wire [3:0] LMask, Mask, ram_1_read_time, ram_1_write_time, RMask;
  wire [6:0] KDB_DATA, TTY_DATA;
  wire [15:0] Addr, LAddr, RAddr;
  wire [31:0] I0, I1, I2, I3, LData, ram_1_data_out_0, ram_1_data_out_1, ram_1_data_out_2, ram_1_data_out_3,
       RI0, RI1, RI2, RI3;

  TTY_part #(.rows(25), .cols(80)) tty_1 (.data(TTY_DATA), .clk(CLK), .we(TTY_EN), .clr(RST));
  not not_1 (LoadRAMOn, ram_dispatcher_1_finished);
  RAM_Dispatcher ram_dispatcher_1 (
    .WriteTime(ram_1_write_time), .Clock(CLK), .Data(LData), .Address(LAddr), .Mask(LMask),
    .Finished(ram_dispatcher_1_finished), .Write(LW), .CLR(LCLR));
  Keyboard #(.buflen(64)) keyboard_1 (.clk(CLK), .re(KDB[0]), .avail(KDB[2]), .data(KDB_DATA));  // open: clr
  RAM ram_1 (
    .Address(RAddr), .Data_Out_0(ram_1_data_out_0), .Data_Out_1(ram_1_data_out_1),
    .Data_Out_2(ram_1_data_out_2), .Data_Out_3(ram_1_data_out_3), .Data_In_0(RI0), .Data_In_1(RI1),
    .Data_In_2(RI2), .Data_In_3(RI3), .Mask(RMask), .nRead_Write(R_R_W), .Chip_Select(RCS),
    .Read_Time(ram_1_read_time), .Reset(button_1_out), .Write_Time(ram_1_write_time));
  Button button_1 (.out(button_1_out));
  D_Flip_Flop d_ff_1 (.clk(CLK), .D(1'b1), .Q(d_ff_1_q), .reset(Reset_out));  // open: Qn, preset, en
  Button Reset (.out(Reset_out));
  S_MIPS s_mips_1 (
    .Kbd_Enable(KDB[0]), .Address(Addr), .Kbd_Clear(KDB[1]), .Kbd_Available(KDB[2]), .RAM_In_0(I0),
    .Kbd_ASCII_Data(KDB_DATA), .RAM_In_1(I1), .TTY_Enable(TTY_EN), .RAM_In_2(I2), .RAM_In_3(I3),
    .TTY_ASCII_Data(TTY_DATA), .Reset(RST), .RAM_Out_0(ram_1_data_out_0), .Clock(CLK),
    .RAM_Out_1(ram_1_data_out_1), .Stop(halt), .RAM_Out_2(ram_1_data_out_2), .RAM_Out_3(ram_1_data_out_3),
    .Mask(Mask), .Read_Time(ram_1_read_time), .Write_Time(ram_1_write_time), .nRead_Write(R_W),
    .Chip_Select(CS));
  D_Flip_Flop d_ff_2 (.clk(CLK), .D(d_ff_1_q), .Qn(LCLR), .reset(Reset_out));  // open: Q, preset, en
  or or_1 (RST, LCLR, LoadRAM);
  Clock clock_1 (.out(CLK));
  Multiplexer #(.width(32), .enable("false")) multiplexer_1 (.in0(I0), .in1(LData), .out(RI0), .sel(LoadRAM));
  Multiplexer #(.width(32), .enable("false")) multiplexer_2 (.in0(I1), .in1(LData), .out(RI1), .sel(LoadRAM));
  Multiplexer #(.width(32), .enable("false")) multiplexer_3 (.in0(I2), .in1(LData), .out(RI2), .sel(LoadRAM));
  Multiplexer #(.width(32), .enable("false")) multiplexer_4 (.in0(I3), .in1(LData), .out(RI3), .sel(LoadRAM));
  and and_1 (LoadRAM, ~DESHABILITAR_DISPATCHER, LoadRAMOn);  // AND_Gate
  Multiplexer #(.width(16), .enable("false")) multiplexer_5 (.in0(Addr), .in1(LAddr), .out(RAddr), .sel(LoadRAM));
  Multiplexer #(.width(4), .enable("false")) multiplexer_6 (.in0(Mask), .in1(LMask), .out(RMask), .sel(LoadRAM));
  Multiplexer #(.enable("false")) multiplexer_7 (.in0(CS), .in1(LW), .out(RCS), .sel(LoadRAM));
  Multiplexer #(.enable("false")) multiplexer_8 (.in0(R_W), .in1(LW), .out(R_R_W), .sel(LoadRAM));

  // Notes on the sheet:
  //   NO MODIFICAR
  //   Keyboard
endmodule

module RAM (
  input  [15:0] Address,
  input  [31:0] Data_In_0,
  input  [31:0] Data_In_1,
  input  [31:0] Data_In_2,
  input  [31:0] Data_In_3,
  input  [3:0] Mask,
  input  nRead_Write,
  input  Chip_Select,
  input  Reset,
  output [31:0] Data_Out_0,
  output [31:0] Data_Out_1,
  output [31:0] Data_Out_2,
  output [31:0] Data_Out_3,
  output [3:0] Read_Time,
  output [3:0] Write_Time
);

  wire and_2_out, and_3_out, and_4_out, and_5_out, and_6_out, and_7_out, and_8_out, and_9_out, Changed, CLK,
       comparator_2_eq, comparator_3_eq, comparator_4_eq, comparator_5_eq, comparator_6_eq, Count,
       demultiplexer_3_out0, Idle, Idle_q, Load, Load0, Load1, nand_1_out, or_1_out, or_2_out, or_3_out,
       or_4_out, or_5_out, or_6_out, or_7_out, or_8_out, or_9_out, or_10_out, Proc_q, Update_Mem, Zero_Time;
  wire [3:0] counter_1_q, multiplexer_1_out, subtractor_1_out;
  wire [31:0] register_1_q, register_2_q, register_3_q, register_4_q, register_5_q;

  // Probe on 4'b0011
  // Probe on 4'b0010
  Multiplexer #(.width(4), .enable("false")) multiplexer_1 (
    .in0(4'b0011), .in1(4'b0010), .out(multiplexer_1_out), .sel(nRead_Write));
  or or_1 (or_1_out, Idle, Update_Mem);
  or or_2 (or_2_out, ~Chip_Select, Reset);  // OR_Gate
  Subtractor #(.width(4)) subtractor_1 (.a(multiplexer_1_out), .b(4'b0010), .out(subtractor_1_out));  // open: bin, bout
  D_Flip_Flop u_Idle (.clk(CLK), .D(or_1_out), .Q(Idle_q), .preset(or_2_out));  // open: Qn, en, reset
  Demultiplexer #(.enable("false")) demultiplexer_1 (.out0(Idle), .out1(Load0), .in(Idle_q), .sel(Changed));
  // Probe on counter_1_q
  Counter #(.width(4), .max('hf)) counter_1 (
    .load(Load), .D(subtractor_1_out), .count(Count), .Q(counter_1_q), .clk(CLK), .clr(or_3_out));  // open: carry
  or or_3 (or_3_out, ~Chip_Select, Reset);  // OR_Gate
  Comparator #(.width(4), .mode("unsigned")) comparator_1 (
    .a(4'b0000), .b(counter_1_q), .eq(Zero_Time));  // open: gt, lt
  or or_4 (or_4_out, Count, Load0, Load1);
  Register #(.width(32)) register_1 (.D(Data_In_0), .en(Chip_Select), .Q(register_1_q), .clk(CLK), .clr(or_5_out));
  or or_5 (or_5_out, ~Chip_Select, Reset);  // OR_Gate
  Register #(.width(32)) register_2 (.D(Data_In_1), .en(Chip_Select), .Q(register_2_q), .clk(CLK), .clr(or_6_out));
  or or_6 (or_6_out, ~Chip_Select, Reset);  // OR_Gate
  Register #(.width(32)) register_3 (.D(Data_In_2), .en(Chip_Select), .Q(register_3_q), .clk(CLK), .clr(or_7_out));
  or or_7 (or_7_out, ~Chip_Select, Reset);  // OR_Gate
  Register #(.width(32)) register_4 (.D(Data_In_3), .en(Chip_Select), .Q(register_4_q), .clk(CLK), .clr(or_8_out));
  or or_8 (or_8_out, ~Chip_Select, Reset);  // OR_Gate
  Register #(.width(32)) register_5 (
    .D({{11{1'b1}}, nRead_Write, Mask, Address}), .en(Chip_Select), .Q(register_5_q), .clk(CLK),
    .clr(or_9_out));
  or or_9 (or_9_out, ~Chip_Select, Reset);  // OR_Gate
  D_Flip_Flop Proc (.clk(CLK), .D(or_4_out), .Q(Proc_q), .reset(or_10_out));  // open: Qn, preset, en
  or or_10 (or_10_out, ~Chip_Select, Reset);  // OR_Gate
  Demultiplexer #(.enable("false")) demultiplexer_2 (
    .out0(Count), .out1(Update_Mem), .in(demultiplexer_3_out0), .sel(Zero_Time));
  Demultiplexer #(.enable("false")) demultiplexer_3 (
    .out0(demultiplexer_3_out0), .out1(Load1), .in(Proc_q), .sel(Changed));
  Clock clock_1 (.out(CLK));
  Comparator #(.width(32)) comparator_2 (.a(register_1_q), .b(Data_In_0), .eq(comparator_2_eq));  // open: gt, lt
  Comparator #(.width(32)) comparator_3 (.a(register_2_q), .b(Data_In_1), .eq(comparator_3_eq));  // open: gt, lt
  Comparator #(.width(32)) comparator_4 (.a(register_3_q), .b(Data_In_2), .eq(comparator_4_eq));  // open: gt, lt
  Comparator #(.width(32)) comparator_5 (.a(register_4_q), .b(Data_In_3), .eq(comparator_5_eq));  // open: gt, lt
  Comparator #(.width(32)) comparator_6 (
    .a(register_5_q), .b({{11{1'b1}}, nRead_Write, Mask, Address}), .eq(comparator_6_eq));  // open: gt, lt
  nand nand_1 (nand_1_out, comparator_6_eq, comparator_2_eq, comparator_3_eq, comparator_4_eq, comparator_5_eq);
  and and_1 (Changed, nand_1_out, Chip_Select);
  or or_11 (Load, Count, Load1, Load0);
  and and_2 (and_2_out, Mask[0], Update_Mem, nRead_Write);
  and and_3 (and_3_out, Mask[1], Update_Mem, nRead_Write);
  and and_4 (and_4_out, Mask[2], Update_Mem, nRead_Write);
  and and_5 (and_5_out, Mask[3], Update_Mem, nRead_Write);
  RAM_part #(.addrWidth(16), .dataWidth(32), .bus("separate")) ram_1 (
    .addr(Address), .din(Data_In_0), .data(Data_Out_0), .str(and_2_out), .sel(Chip_Select), .clk(CLK),
    .ld(and_6_out), .clr(Reset));
  and and_6 (and_6_out, ~nRead_Write, Idle);  // AND_Gate
  RAM_part #(.addrWidth(16), .dataWidth(32), .bus("separate")) ram_2 (
    .addr(Address), .din(Data_In_1), .data(Data_Out_1), .str(and_3_out), .sel(Chip_Select), .clk(CLK),
    .ld(and_7_out), .clr(Reset));
  and and_7 (and_7_out, ~nRead_Write, Idle);  // AND_Gate
  RAM_part #(.addrWidth(16), .dataWidth(32), .bus("separate")) ram_3 (
    .addr(Address), .din(Data_In_2), .data(Data_Out_2), .str(and_4_out), .sel(Chip_Select), .clk(CLK),
    .ld(and_8_out), .clr(Reset));
  and and_8 (and_8_out, ~nRead_Write, Idle);  // AND_Gate
  RAM_part #(.addrWidth(16), .dataWidth(32), .bus("separate")) ram_4 (
    .addr(Address), .din(Data_In_3), .data(Data_Out_3), .str(and_5_out), .sel(Chip_Select), .clk(CLK),
    .ld(and_9_out), .clr(Reset));
  and and_9 (and_9_out, ~nRead_Write, Idle);  // AND_Gate

  assign Read_Time = 4'b0011;
  assign Write_Time = 4'b0010;

  // Other names for the same wires on the sheet: M0 = Mask[0]; M1 = Mask[1]; M2 = Mask[2]; M3 = Mask[3];
  //   RW = nRead_Write; CLR = Reset; CS = Chip_Select; Load2 = Count

  // Notes on the sheet:
  //   NO MODIFICAR
  //   excepto quizás los valores RT y WT
  //   BANK0
  //   BANK1
  //   BANK2
  //   BANK3
endmodule

module S_MIPS (
  input  Kbd_Available,
  input  [6:0] Kbd_ASCII_Data,
  input  Reset,
  input  [31:0] RAM_Out_0,
  input  Clock,
  input  [31:0] RAM_Out_1,
  input  [31:0] RAM_Out_2,
  input  [31:0] RAM_Out_3,
  input  [3:0] Read_Time,
  input  [3:0] Write_Time,
  output Kbd_Enable,
  output [15:0] Address,
  output Kbd_Clear,
  output TTY_Enable,
  output [6:0] TTY_ASCII_Data,
  output Stop,
  output [31:0] RAM_In_0,
  output [31:0] RAM_In_1,
  output [31:0] RAM_In_2,
  output [31:0] RAM_In_3,
  output [3:0] Mask,
  output nRead_Write,
  output Chip_Select
);

  wire e_ALU_I, e_ALU_R, e_KBD, e_Lw_Sw, e_PC, e_Push_Pop, e_Read_RF, e_write_Hi_Low, e_write_RF,
       EN_DMux_Ram_In, Guardar_Lectura_Ram, Guardar_Lectura_Ram_esp, leer_inicio, mul___div_ALU, s_Push_Pop;
  wire [1:0] mask_2, mask_2_esp, multiplexer_4_out, s_Address, s_BC, s_Ram_In, s_Write_RF;
  wire [2:0] s_Input_RF;
  wire [3:0] mask_4_especial, RAM_MASK;
  wire [4:0] Rd, Rs, Rt;
  wire [5:0] Func_Code, Op_Code;
  wire [15:0] Add_especial, Const, RAM_A;
  wire [25:0] Destino;
  wire [31:0] demultiplexer_1_out0, demultiplexer_1_out1, demultiplexer_1_out2, demultiplexer_1_out3, Input,
       inversor_1_output, inversor_2_output, inversor_3_output, inversor_4_output, multiplexer_3_out, Ram_In,
       Ram_out, register_3_q;

  Multiplexer #(.width(16), .enable("false")) multiplexer_1 (
    .in0(Add_especial), .in1(RAM_A), .out(Address), .sel(leer_inicio));
  Multiplexer #(.width(4), .enable("false")) multiplexer_2 (
    .in0(mask_4_especial), .in1(RAM_MASK), .out(Mask), .sel(leer_inicio));
  Control_Unit control_unit_1 (
    .in_1(Input), .in_2(Clock), .in_3(Reset), .in_4(Read_Time), .in_5(Write_Time), .in_6(mul___div_ALU),
    .out_19(e_write_RF), .out_7(Func_Code), .out_9(Stop), .out_18(e_ALU_I), .out_10(Rs),
    .selectores(s_Input_RF), .out_26(e_write_Hi_Low), .out_15(Rt), .out_11(s_BC), .out_23(e_Lw_Sw),
    .out_20(Rd), .out_12(Chip_Select), .out_14(e_ALU_R), .out_17(nRead_Write), .out_25(Const),
    .out_32(Destino), .out_13(e_PC), .out_16(s_Write_RF), .out_33(TTY_Enable), .out_36(e_KBD),
    .out_30(e_Push_Pop), .out_21(s_Address), .out_24(s_Push_Pop), .out_29(e_Read_RF), .out_28(s_Ram_In),
    .out_22(TTY_Enable), .out_27(leer_inicio), .out_31(Guardar_Lectura_Ram), .out_37(Op_Code),
    .out_35(Guardar_Lectura_Ram_esp), .out_34(EN_DMux_Ram_In));
  Inversor inversor_1 (.in_1(RAM_Out_0), .Output(inversor_1_output));
  Inversor inversor_2 (.in_1(RAM_Out_1), .Output(inversor_2_output));
  Inversor inversor_3 (.in_1(RAM_Out_2), .Output(inversor_3_output));
  Inversor inversor_4 (.in_1(RAM_Out_3), .Output(inversor_4_output));
  Multiplexer #(.select(2), .width(32)) multiplexer_3 (
    .in0(inversor_1_output), .in1(inversor_2_output), .in2(inversor_3_output), .in3(inversor_4_output),
    .out(multiplexer_3_out), .sel(multiplexer_4_out));  // open: en
  // Probe on multiplexer_4_out
  Multiplexer #(.width(2), .enable("false")) multiplexer_4 (
    .in0(mask_2_esp), .in1(mask_2), .out(multiplexer_4_out), .sel(leer_inicio));
  // Probe on inversor_1_output
  // Probe on multiplexer_3_out
  Register #(.width(32)) register_1 (
    .D(multiplexer_3_out), .en(Guardar_Lectura_Ram), .Q(Input), .clk(Clock), .clr(Reset));
  // Probe on Guardar_Lectura_Ram
  // Probe on Input
  Inversor inversor_5 (.in_1(demultiplexer_1_out0), .Output(RAM_In_0));
  Inversor inversor_6 (.in_1(demultiplexer_1_out1), .Output(RAM_In_1));
  Inversor inversor_7 (.in_1(demultiplexer_1_out2), .Output(RAM_In_2));
  Inversor inversor_8 (.in_1(demultiplexer_1_out3), .Output(RAM_In_3));
  Register #(.width(32)) register_2 (
    .D(multiplexer_3_out), .en(Guardar_Lectura_Ram_esp), .Q(Ram_out), .clk(Clock), .clr(Reset));
  Data_Path data_path_1 (
    .in_1(Clock), .in_2(Reset), .in_3(Func_Code), .Selectores(s_Input_RF), .in_5(Rs), .in_9(e_write_RF),
    .in_7(s_Write_RF), .in_8(Rt), .in_10(s_BC), .in_11(Ram_out), .in_12(Rd), .in_15(e_write_Hi_Low),
    .in_6(e_PC), .in_18(Const), .in_23(Destino), .mul___div(mul___div_ALU), .in_19(e_ALU_I), .in_13(e_ALU_R),
    .out_29(TTY_ASCII_Data), .in_21(TTY_Enable), .in_24(Kbd_Available), .in_17(Kbd_Available),
    .in_20(Kbd_ASCII_Data), .in_25(e_Lw_Sw), .out_30(RAM_A), .Output(RAM_MASK), .Output_2(mask_2),
    .in_14(s_Address), .in_16(s_Push_Pop), .in_22(s_Ram_In), .Ram_in(Ram_In), .KBD_Enable(Kbd_Enable),
    .in_26(Op_Code), .out_32(Add_especial), .Output_3(mask_4_especial), .Output_4(mask_2_esp));
  Demultiplexer #(.select(2), .width(32)) demultiplexer_1 (
    .out0(demultiplexer_1_out0), .out1(demultiplexer_1_out1), .out2(demultiplexer_1_out2),
    .out3(demultiplexer_1_out3), .in(register_3_q), .sel(mask_2_esp));  // open: en
  // Probe on mask_2_esp
  // Probe on Ram_out
  // Probe on register_3_q
  Register #(.width(32)) register_3 (.D(Ram_In), .en(EN_DMux_Ram_In), .Q(register_3_q), .clk(Clock), .clr(Reset));

  // Other names for the same wires on the sheet: CLK = Clock; CLR = Reset; CS = Chip_Select;
  //   KBD_AVAIL = Kbd_Available; KBD_CLR = Kbd_Clear; KBD_DATA[6:0] = Kbd_ASCII_Data; RAM_INPUT_0[31:0] = RAM_In_0;
  //   RAM_INPUT_1[31:0] = RAM_In_1; RAM_INPUT_2[31:0] = RAM_In_2; RAM_INPUT_3[31:0] = RAM_In_3;
  //   RAM_OUTPUT_0[31:0] = RAM_Out_0; RAM_OUTPUT_1[31:0] = RAM_Out_1; RAM_OUTPUT_2[31:0] = RAM_Out_2;
  //   RAM_OUTPUT_3[31:0] = RAM_Out_3; RW = nRead_Write; TTY_DATA[6:0] = TTY_ASCII_Data

  // Notes on the sheet:
  //   RAM ADDRESS
  //   DATA TO RAM
  //   RAM TIMING
  //   RAM CONTROL
  //   DATA FROM RAM
  //   DATA WRITE MASK
  //   KEYBOARD
  //   TTY
  //   SEQUENCING
endmodule

module RAM_Dispatcher (
  input  [3:0] WriteTime,
  input  Clock,
  input  CLR,
  output [31:0] Data,
  output [15:0] Address,
  output [3:0] Mask,
  output Finished,
  output Write
);

  wire demultiplexer_2_out1, demultiplexer_3_out1, End, IDLE_q, IncAddr, Load, or_1_out, or_2_out, While_q,
       WriteEnd;
  wire [3:0] counter_1_q;
  wire [31:0] CurrentAddress_q;

  Counter #(.width(32), .max('hffffffff)) CurrentAddress (
    .count(IncAddr), .Q({CurrentAddress_q[31:18], Address, CurrentAddress_q[1:0]}), .clk(Clock), .clr(CLR));  // open: load, D, carry
  or or_1 (or_1_out, IncAddr, demultiplexer_3_out1, Finished);
  D_Flip_Flop IDLE (.clk(Clock), .D(or_1_out), .Q(IDLE_q), .preset(CLR));  // open: Qn, en, reset
  Demultiplexer #(.enable("false")) demultiplexer_1 (.out0(Load), .out1(Finished), .in(IDLE_q), .sel(End));
  D_Flip_Flop While (.clk(Clock), .D(or_2_out), .Q(While_q), .reset(CLR));  // open: Qn, preset, en
  or or_2 (or_2_out, Write, Load);
  RAM_part #(.addrWidth(18), .dataWidth(32)) ram_1 (
    .addr({Address, CurrentAddress_q[1:0]}), .data(Data), .clk(Clock));  // open: sel, ld, clr
  Demultiplexer #(.enable("false")) demultiplexer_2 (
    .out0(Write), .out1(demultiplexer_2_out1), .in(While_q), .sel(WriteEnd));
  Decoder #(.select(2)) decoder_1 (
    .out0(Mask[0]), .out1(Mask[1]), .out2(Mask[2]), .out3(Mask[3]), .sel(CurrentAddress_q[1:0]));  // open: en
  Demultiplexer #(.enable("false")) demultiplexer_3 (
    .out0(IncAddr), .out1(demultiplexer_3_out1), .in(demultiplexer_2_out1), .sel(End));
  Counter #(.width(4), .max('hf)) counter_1 (
    .load(Load), .D(WriteTime), .count(Write), .Q(counter_1_q), .clk(Clock));  // open: carry, clr
  Comparator #(.width(32)) comparator_1 (.a(Data), .b({32{1'b1}}), .eq(End));  // open: gt, lt
  Comparator #(.width(4)) comparator_2 (.a(4'b0000), .b(counter_1_q), .eq(WriteEnd));  // open: gt, lt

  // Other names for the same wires on the sheet: CLK = Clock; Count = Write; WT[3:0] = WriteTime
endmodule

module Instruction_Decoder (
  input  [31:0] in_1,
  output [4:0] Rt,
  output [15:0] Constante,
  output [5:0] Op_Code,
  output [5:0] Func_Code,
  output [4:0] Rd,
  output [4:0] Rs,
  output [4:0] x,
  output [25:0] Destino_salto,
  output out_10,
  output out_11,
  output out_12,
  output out_13,
  output out_14,
  output out_15,
  output out_16,
  output out_17,
  output out_18,
  output out_19,
  output out_20,
  output out_21,
  output out_22
);

  wire comparator_2_eq, comparator_3_eq, comparator_4_eq, comparator_5_eq, comparator_6_eq, comparator_7_eq,
       comparator_8_eq, I, IE, nor_1_out, nor_3_out, or_1_out, R, r_I_J, r_I_Ram;

  Comparator #(.width(32)) comparator_1 (.a(in_1), .b({32{1'b0}}), .eq(out_20));  // open: gt, lt
  Comparator #(.width(6)) comparator_2 (.a(in_1[5:0]), .b(6'b001000), .eq(comparator_2_eq));  // open: gt, lt
  Comparator #(.width(6)) comparator_3 (.a(in_1[5:0]), .b(6'b010000), .eq(comparator_3_eq));  // open: gt, lt
  Comparator #(.width(6)) comparator_4 (.a(in_1[5:0]), .b(6'b010010), .eq(comparator_4_eq));  // open: gt, lt
  Comparator #(.width(6)) comparator_5 (.a(in_1[5:0]), .b({6{1'b1}}), .eq(comparator_5_eq));  // open: gt, lt
  Comparator #(.width(6)) comparator_6 (.a(in_1[5:0]), .b(6'b000001), .eq(comparator_6_eq));  // open: gt, lt
  and and_1 (out_17, comparator_2_eq, R);
  or or_1 (or_1_out, comparator_3_eq, comparator_4_eq);
  and and_2 (out_14, comparator_5_eq, IE);
  and and_3 (out_21, comparator_6_eq, IE);
  and and_4 (out_11, or_1_out, R);
  Comparator #(.width(6)) comparator_7 (.a(in_1[5:0]), .b(6'b000010), .eq(comparator_7_eq));  // open: gt, lt
  Comparator #(.width(6)) comparator_8 (.a(in_1[5:0]), .b(6'b000100), .eq(comparator_8_eq));  // open: gt, lt
  nor nor_1 (nor_1_out, out_17, out_20, out_11);
  and and_5 (out_10, nor_1_out, R);
  and and_6 (out_15, comparator_7_eq, IE);
  and and_7 (out_22, comparator_8_eq, IE);
  Comparator #(.width(6)) comparator_9 (.a(in_1[31:26]), .b({6{1'b0}}), .eq(R));  // open: gt, lt
  Comparator #(.width(6)) comparator_10 (.a(in_1[31:26]), .b(6'b000010), .eq(out_13));  // open: gt, lt
  Comparator #(.width(6)) comparator_11 (.a(in_1[31:26]), .b(6'b111000), .eq(out_16));  // open: gt, lt
  Comparator #(.width(6)) comparator_12 (.a(in_1[31:26]), .b({6{1'b1}}), .eq(IE));  // open: gt, lt
  nor nor_2 (I, R, out_13, out_16, IE);
  Comparator #(.width(3)) comparator_13 (.a(in_1[31:29]), .b(3'b000), .eq(r_I_J));  // open: gt, lt
  and and_8 (out_19, I, r_I_J);
  Comparator #(.width(3)) comparator_14 (.a(in_1[28:26]), .b(3'b011), .eq(r_I_Ram));  // open: gt, lt
  and and_9 (out_18, I, r_I_Ram);
  nor nor_3 (nor_3_out, out_19, out_18);
  and and_10 (out_12, nor_3_out, I);

  assign Constante = in_1[15:0];
  assign Destino_salto = in_1[25:0];
  assign Func_Code = in_1[5:0];
  assign Op_Code = in_1[31:26];
  assign Rd = in_1[15:11];
  assign Rs = in_1[25:21];
  assign Rt = in_1[20:16];
  assign x = in_1[10:6];

  // Other names for the same wires on the sheet: halt = out_14; I_J = out_19; I_Ram = out_18; I_RF = out_12;
  //   Input[31:0] = in_1; J = out_13; kbd = out_22; nop = out_20; P = out_16; R_ALU = out_10; R_jr = out_17;
  //   R_mfhi_mflo = out_11; rnd = out_15; tty = out_21

  // Notes on the sheet:
  //   nop
  //   jr
  //   mflo / mfhi
  //   Instruction Decoder
  //   R-ALU
  //   Tipo R
  //   Tipo I
  //   I-Jump
  //   I-Ram
  //   I-ALU-I
  //   Tipo de instruccion
endmodule

module ALU_R (
  input  [5:0] in_1,
  input  in_2,
  input  [31:0] in_3,
  input  [31:0] in_4,
  input  [15:0] in_5,
  output Output,
  output [31:0] low,
  output [31:0] hi
);

  wire add, \and , con_signo, div, divu, mul, mulu, \nor , \or , rnd, slt, sltu, sub, \xor ;
  wire [3:0] priority_encoder_1_out, priority_encoder_2_out;
  wire [31:0] div__divu_hi, div__divu_lo, mult___mulu_hi, mult___mulu_lo, s_add, s_and, s_nor, s_or, s_rnd,
       s_sub, s_xor, slt___sltu;

  // Probe on in_1[0]
  not not_1 (con_signo, in_1[0]);
  Adder #(.width(32)) adder_1 (.a(in_3), .b(in_4), .out(s_add));  // open: cin, cout
  Subtractor #(.width(32)) subtractor_1 (.a(in_3), .b(in_4), .out(s_sub));  // open: bin, bout
  assign s_and = in_3 & in_4;  // AND_Gate and_1, 32 bits wide
  assign s_or = in_3 | in_4;  // OR_Gate or_1, 32 bits wide
  assign s_xor = in_3 ^ in_4;  // XOR_Gate xor_1, 32 bits wide
  assign s_nor = ~(in_3 | in_4);  // NOR_Gate nor_1, 32 bits wide
  and and_2 (add, ~in_1[0], ~in_1[1], ~in_1[2], ~in_1[3], ~in_1[4], in_1[5]);  // AND_Gate
  and and_3 (sub, ~in_1[0], in_1[1], ~in_1[2], ~in_1[3], ~in_1[4], in_1[5]);  // AND_Gate
  and and_4 (mul, ~in_1[0], ~in_1[1], ~in_1[2], in_1[3], in_1[4], ~in_1[5]);  // AND_Gate
  and and_5 (mulu, in_1[0], ~in_1[1], ~in_1[2], in_1[3], in_1[4], ~in_1[5]);  // AND_Gate
  Priority_Encoder #(.select(4)) priority_encoder_1 (
    .in0(add), .in1(sub), .in2(mul), .in3(mulu), .in4(div), .in5(divu), .in6(slt), .in7(sltu), .in8(\and ),
    .in9(\or ), .in10(\nor ), .in11(\xor ), .in12(rnd), .out(priority_encoder_1_out));  // open: in13, in14, in15, gs, en_out, en_in
  Priority_Encoder #(.select(4)) priority_encoder_2 (
    .in0(add), .in1(sub), .in2(mul), .in3(mulu), .in4(div), .in5(divu), .in6(slt), .in7(sltu), .in8(\and ),
    .in9(\or ), .in10(\nor ), .in11(\xor ), .in12(rnd), .out(priority_encoder_2_out));  // open: in13, in14, in15, gs, en_out, en_in
  div___divu div_divu_1 (.in_1(in_3), .in_2(in_4), .in_3(con_signo), .Hi(div__divu_hi), .Lo(div__divu_lo));
  slt___sltu slt_sltu_1 (.Rt(in_4), .Rs(in_3), .Output(slt___sltu), .in_1(con_signo));
  // Probe on priority_encoder_1_out
  // Probe on priority_encoder_2_out
  and and_6 (div, ~in_1[0], in_1[1], ~in_1[2], in_1[3], in_1[4], ~in_1[5]);  // AND_Gate
  and and_7 (divu, in_1[0], in_1[1], ~in_1[2], in_1[3], in_1[4], ~in_1[5]);  // AND_Gate
  and and_8 (slt, ~in_1[0], in_1[1], ~in_1[2], in_1[3], ~in_1[4], in_1[5]);  // AND_Gate
  and and_9 (sltu, in_1[0], in_1[1], ~in_1[2], in_1[3], ~in_1[4], in_1[5]);  // AND_Gate
  mult___mulu mult_mulu_1 (.in_1(in_3), .in_2(in_4), .in_3(con_signo), .hi(mult___mulu_hi), .lo(mult___mulu_lo));
  Random #(.width(32)) random_1 (.out(s_rnd));  // open: clk, next, clr
  and and_10 (\and , ~in_1[0], ~in_1[1], in_1[2], ~in_1[3], ~in_1[4], in_1[5]);  // AND_Gate
  and and_11 (\or , in_1[0], ~in_1[1], in_1[2], ~in_1[3], ~in_1[4], in_1[5]);  // AND_Gate
  and and_12 (\nor , in_1[0], in_1[1], in_1[2], ~in_1[3], ~in_1[4], in_1[5]);  // AND_Gate
  and and_13 (\xor , ~in_1[0], ~in_1[1], ~in_1[2], in_1[3], ~in_1[4], in_1[5]);  // AND_Gate
  Multiplexer #(.select(4), .width(32)) multiplexer_1 (
    .in0(s_add), .in1(s_sub), .in2(mult___mulu_lo), .in3(mult___mulu_lo), .in4(div__divu_lo),
    .in5(div__divu_lo), .in6(slt___sltu), .in7(slt___sltu), .in8(s_and), .in9(s_or), .in10(s_nor),
    .in11(s_xor), .in12(s_rnd), .out(low), .sel(priority_encoder_1_out), .en(in_2));  // open: in13, in14, in15
  Multiplexer #(.select(4), .width(32)) multiplexer_2 (
    .in0({32{1'b0}}), .in1({32{1'b0}}), .in2(mult___mulu_hi), .in3(mult___mulu_hi), .in4(div__divu_hi),
    .in5(div__divu_hi), .in6({32{1'b0}}), .in7({32{1'b0}}), .in8({32{1'b0}}), .in9({32{1'b0}}),
    .in10({32{1'b0}}), .in11({32{1'b0}}), .in12({32{1'b0}}), .out(hi), .sel(priority_encoder_2_out), .en(in_2));  // open: in13, in14, in15
  or or_2 (Output, mul, mulu, div, divu);
  and and_14 (rnd, ~in_1[0], in_1[1], ~in_1[2], ~in_1[3], ~in_1[4], ~in_1[5]);  // AND_Gate

  // Other names for the same wires on the sheet: Const[15:0] = in_5; EN = in_2; Func_Code[5:0] = in_1;
  //   Rs[31:0] = in_3; Rt[31:0] = in_4

  // Notes on the sheet:
  //   add
  //   sub
  //   mul
  //   mulu
  //   Tipo R
  //   div
  //   divu
  //   slt
  //   sltu
  //   Calculos
  //   div divu
  //   and
  //   or
  //   nor
  //   xor
  //   rnd
endmodule

module div___divu (
  input  [31:0] in_1,
  input  [31:0] in_2,
  input  in_3,
  output [31:0] Lo,
  output [31:0] Hi
);

  wire [31:0] div_a_negativo, div_b_negativo, div_negativos, div_positivos, divider_2_out, divider_3_out,
       Hi_sin_sg, Lo_sin_sg, minus_a, minus_b, resto_a_negativo, resto_b_negativo, resto_negativo,
       resto_positivo;

  Divider #(.width(32)) divider_1 (.a(in_1), .b(in_2), .out(div_positivos), .rem(resto_positivo));  // open: upper
  Divider #(.width(32)) divider_2 (.a(minus_a), .b(in_2), .out(divider_2_out), .rem(resto_a_negativo));  // open: upper
  Negator #(.width(32)) negator_1 (.in(divider_2_out), .out(div_a_negativo));
  Divider #(.width(32)) divider_3 (.a(in_1), .b(minus_b), .out(divider_3_out), .rem(resto_b_negativo));  // open: upper
  Negator #(.width(32)) negator_2 (.in(divider_3_out), .out(div_b_negativo));
  Divider #(.width(32)) divider_4 (.a(minus_a), .b(minus_b), .out(div_negativos), .rem(resto_negativo));  // open: upper
  // Probe on in_1
  Negator #(.width(32)) negator_3 (.in(in_1), .out(minus_a));
  // Probe on in_2
  Negator #(.width(32)) negator_4 (.in(in_2), .out(minus_b));
  // Probe on Lo
  Multiplexer #(.select(2), .width(32)) multiplexer_1 (
    .in0(div_positivos), .in1(div_a_negativo), .in2(div_b_negativo), .in3(div_negativos), .out(Lo_sin_sg),
    .sel({in_2[31], in_1[31]}));  // open: en
  Multiplexer #(.select(2), .width(32)) multiplexer_2 (
    .in0(resto_positivo), .in1(resto_a_negativo), .in2(resto_b_negativo), .in3(resto_negativo),
    .out(Hi_sin_sg), .sel({in_2[31], in_1[31]}));  // open: en
  // Probe on Hi
  Multiplexer #(.width(32), .enable("false")) multiplexer_3 (
    .in0(div_positivos), .in1(Lo_sin_sg), .out(Lo), .sel(in_3));
  Multiplexer #(.width(32), .enable("false")) multiplexer_4 (
    .in0(resto_positivo), .in1(Hi_sin_sg), .out(Hi), .sel(in_3));

  // Other names for the same wires on the sheet: a[31:0] = in_1; b[31:0] = in_2; con_sig = in_3; a_sig = in_1[31];
  //   selector[1:0] = {in_2[31], in_1[31]}; b_sg = in_2[31]

  // Notes on the sheet:
  //   0 : sin signo
  //   1 : con signo
endmodule

module mult___mulu (
  input  [31:0] in_1,
  input  [31:0] in_2,
  input  in_3,
  output [31:0] hi,
  output [31:0] lo
);

  wire [31:0] minus_a, minus_b, mult_hi, mult_lo, multiplexer_1_out, multiplexer_2_out, mulu_Hi, mulu_Lo,
       negator_1_out, negator_2_out;

  Multiplier #(.width(32)) multiplier_1 (.a(in_1), .b(in_2), .out(mult_lo), .cout(mult_hi));  // open: cin
  Negator #(.width(32)) negator_1 (.in(in_1), .out(negator_1_out));
  Negator #(.width(32)) negator_2 (.in(in_2), .out(negator_2_out));
  // Probe on in_1
  // Probe on multiplexer_1_out
  Multiplexer #(.width(32), .enable("false")) multiplexer_1 (
    .in0(in_1), .in1(negator_1_out), .out(multiplexer_1_out), .sel(in_1[31]));
  Multiplexer #(.width(32), .enable("false")) multiplexer_2 (
    .in0(in_2), .in1(negator_2_out), .out(multiplexer_2_out), .sel(in_2[31]));
  Negator #(.width(32)) negator_3 (.in(in_1), .out(minus_a));
  Multiplier #(.width(32)) multiplier_2 (
    .a(multiplexer_1_out), .b(multiplexer_2_out), .out(mulu_Lo), .cout(mulu_Hi));  // open: cin
  // Probe on multiplexer_2_out
  // Probe on in_2
  Negator #(.width(32)) negator_4 (.in(in_2), .out(minus_b));
  // Probe on lo
  // Probe on hi
  Multiplexer #(.width(32), .enable("false")) multiplexer_3 (.in0(mult_hi), .in1(mulu_Hi), .out(hi), .sel(in_3));
  Multiplexer #(.width(32), .enable("false")) multiplexer_4 (.in0(mult_lo), .in1(mulu_Lo), .out(lo), .sel(in_3));

  // Other names for the same wires on the sheet: a[31:0] = in_1; a_sig = in_1[31]; b[31:0] = in_2; b_sg = in_2[31];
  //   con_sig = in_3

  // Notes on the sheet:
  //   0 : sin signo
  //   1 : con signo
endmodule

module Multiplexer_6_bits_32 (
  input  [31:0] in_1,
  input  [31:0] in_2,
  input  [31:0] in_3,
  input  [31:0] in_4,
  input  [31:0] in_5,
  input  [31:0] in_6,
  input  [31:0] in_7,
  input  [31:0] in_8,
  input  [31:0] in_9,
  input  [31:0] in_10,
  input  [31:0] in_11,
  input  [31:0] in_12,
  input  [31:0] in_13,
  input  [31:0] in_14,
  input  [31:0] in_15,
  input  [31:0] in_16,
  input  [31:0] in_17,
  input  [31:0] in_18,
  input  [31:0] in_19,
  input  [31:0] in_20,
  input  [31:0] in_21,
  input  [31:0] in_22,
  input  [31:0] in_23,
  input  [31:0] in_24,
  input  [31:0] in_25,
  input  [31:0] in_26,
  input  [31:0] in_27,
  input  [31:0] in_28,
  input  [31:0] in_29,
  input  [31:0] in_30,
  input  [31:0] in_31,
  input  [31:0] in_32,
  input  [31:0] in_33,
  input  [31:0] in_34,
  input  [31:0] in_35,
  input  [31:0] in_36,
  input  [31:0] in_37,
  input  [31:0] in_38,
  input  [31:0] in_39,
  input  [31:0] in_40,
  input  [31:0] in_41,
  input  [31:0] in_42,
  input  [31:0] in_43,
  input  [31:0] in_44,
  input  [31:0] in_45,
  input  [31:0] in_46,
  input  [31:0] in_47,
  input  [31:0] in_48,
  input  [31:0] in_49,
  input  [31:0] in_50,
  input  [31:0] in_51,
  input  [31:0] in_52,
  input  [31:0] in_53,
  input  [31:0] in_54,
  input  [31:0] in_55,
  input  [31:0] in_56,
  input  [31:0] in_57,
  input  [31:0] in_58,
  input  [31:0] in_59,
  input  [31:0] in_60,
  input  [31:0] in_61,
  input  [31:0] in_62,
  input  [31:0] in_63,
  input  [31:0] in_64,
  output [31:0] S
);

  wire [31:0] S1, S2;

  Multiplexer #(.select(5), .width(32)) multiplexer_1 (
    .in0(in_1), .in1(in_2), .in2(in_3), .in3(in_4), .in4(in_5), .in5(in_6), .in6(in_7), .in7(in_8),
    .in8(in_9), .in9(in_10), .in10(in_11), .in11(in_12), .in12(in_13), .in13(in_14), .in14(in_15),
    .in15(in_16), .in16(in_17), .in17(in_18), .in18(in_19), .in19(in_20), .in20(in_21), .in21(in_22),
    .in22(in_23), .in23(in_24), .in24(in_25), .in25(in_26), .in26(in_27), .in27(in_28), .in28(in_29),
    .in29(in_30), .in30(in_31), .in31(in_32), .out(S1));  // open: sel, en
  Multiplexer #(.select(5), .width(32)) multiplexer_2 (
    .in0(in_33), .in1(in_35), .in2(in_35), .in3(in_36), .in4(in_37), .in5(in_38), .in6(in_39), .in7(in_40),
    .in8(in_41), .in9(in_42), .in10(in_43), .in11(in_44), .in12(in_45), .in13(in_46), .in14(in_47),
    .in15(in_48), .in16(in_49), .in17(in_50), .in18(in_51), .in19(in_52), .in20(in_53), .in21(in_54),
    .in22(in_55), .in23(in_56), .in24(in_57), .in25(in_58), .in26(in_59), .in27(in_60), .in28(in_61),
    .in29(in_62), .in30(in_63), .in31(in_64), .out(S2));  // open: sel, en
  Multiplexer #(.select(2), .width(32)) multiplexer_3 (.in0(S1), .in3(S2), .out(S));  // open: in1, in2, sel, en

  // Other names for the same wires on the sheet: _1[31:0] = in_1; _2[31:0] = in_2; _3[31:0] = in_3; _4[31:0] = in_4;
  //   _5[31:0] = in_5; _6[31:0] = in_6; _7[31:0] = in_7; _8[31:0] = in_8; _9[31:0] = in_9; _10[31:0] = in_10;
  //   _11[31:0] = in_11; _12[31:0] = in_12; _13[31:0] = in_13; _14[31:0] = in_14; _15[31:0] = in_15;
  //   _16[31:0] = in_16; _17[31:0] = in_17; _18[31:0] = in_18; _19[31:0] = in_19; _20[31:0] = in_20;
  //   _21[31:0] = in_21; _22[31:0] = in_22; _23[31:0] = in_23; _24[31:0] = in_24; _25[31:0] = in_25;
  //   _26[31:0] = in_26; _27[31:0] = in_27; _28[31:0] = in_28; _29[31:0] = in_29; _30[31:0] = in_30;
  //   _31[31:0] = in_31; _32[31:0] = in_32; _33[31:0] = in_33; _34[31:0] = in_34; _35[31:0] = in_35;
  //   _36[31:0] = in_36; _37[31:0] = in_37; _38[31:0] = in_38; _39[31:0] = in_39; _40[31:0] = in_40;
  //   _41[31:0] = in_41; _42[31:0] = in_42; _43[31:0] = in_43; _44[31:0] = in_44; _45[31:0] = in_45;
  //   _46[31:0] = in_46; _47[31:0] = in_47; _48[31:0] = in_48; _49[31:0] = in_49; _50[31:0] = in_50;
  //   _51[31:0] = in_51; _52[31:0] = in_52; _53[31:0] = in_53; _54[31:0] = in_54; _55[31:0] = in_55;
  //   _56[31:0] = in_56; _57[31:0] = in_57; _58[31:0] = in_58; _59[31:0] = in_59; _60[31:0] = in_60;
  //   _61[31:0] = in_61; _62[31:0] = in_62; _63[31:0] = in_63; _64[31:0] = in_64
endmodule

module Data_Path (
  input  in_1,
  input  in_2,
  input  [5:0] in_3,
  input  [2:0] Selectores,
  input  [4:0] in_5,
  input  in_6,
  input  [1:0] in_7,
  input  [4:0] in_8,
  input  in_9,
  input  [1:0] in_10,
  input  [31:0] in_11,
  input  [4:0] in_12,
  input  in_13,
  input  [1:0] in_14,
  input  in_15,
  input  in_16,
  input  in_17,
  input  [15:0] in_18,
  input  in_19,
  input  [6:0] in_20,
  input  in_21,
  input  [1:0] in_22,
  input  [25:0] in_23,
  input  in_24,
  input  in_25,
  input  [5:0] in_26,
  output mul___div,
  output [31:0] Ram_in,
  output [6:0] out_29,
  output [15:0] out_30,
  output [3:0] Output,
  output [15:0] out_32,
  output [1:0] Output_2,
  output [3:0] Output_3,
  output KBD_Enable,
  output [1:0] Output_4
);

  wire [1:0] mask_2_lw_sw, mask_2_push_pop;
  wire [3:0] mask_4_lw_sw, mask_4_push_pop;
  wire [4:0] sobreescribir;
  wire [15:0] Addres_lw_sw, Addres_push_pop;
  wire [31:0] A, B, BC, Hi, Hi_ALU, Input, kbd, Low, Low_ALU, multiplexer_1_out, out_I, PC, Push_Pop, SP;

  // Probe on BC
  Multiplexer #(.select(2), .width(32), .enable("false")) multiplexer_1 (
    .in0({PC[31:20], out_30, Output_2, PC[1:0]}), .in1({PC[31:20], out_30, Output_2, PC[1:0]}), .in2(A),
    .in3(out_I), .out(multiplexer_1_out), .sel(in_10));
  Push_Pop push_pop_1 (
    .in_1({SP[31:20], Addres_push_pop, mask_2_push_pop, SP[1:0]}), .Output(Push_Pop), .in_2(in_16));  // open: Mask, Mask_2, Addres
  // Probe on {PC[31:20], out_30, Output_2, PC[1:0]}
  Register #(.width(32)) register_1 (
    .D(BC), .en(in_6), .Q({PC[31:20], out_30, Output_2, PC[1:0]}), .clk(in_1), .clr(in_2));
  // Probe on in_26
  Branch_Control branch_control_1 (
    .in_2(multiplexer_1_out), .in_3(in_23), .in_1(in_6), .in_4(in_10), .Output(BC),
    .in_5({PC[31:20], out_30, Output_2, PC[1:0]}));
  Multiplexer #(.select(2), .width(16)) multiplexer_2 (
    .in0(Addres_lw_sw), .in1(Addres_push_pop), .out(out_32), .sel(in_14));  // open: in2, in3, en
  ALU_I alu_i_1 (.in_1(in_26), .in_3(A), .in_4(in_18), .in_5(B), .Output(out_I));  // open: in_2
  Decoder #(.select(2)) decoder_1 (
    .out0(mask_4_push_pop[0]), .out1(mask_4_push_pop[1]), .out2(mask_4_push_pop[2]),
    .out3(mask_4_push_pop[3]), .sel(mask_2_push_pop));  // open: en
  Register_File register_file_1 (
    .in_1(Input), .in_2(in_9), .in_4(sobreescribir), .in_3(in_5), .in_6(in_2), .in_5(in_8), .in_7(in_1),
    .Sa(A), .Sb(B), .in_8(in_9), .SP({SP[31:20], Addres_push_pop, mask_2_push_pop, SP[1:0]}));
  lw___sw lw_sw_1 (.Rs(A), .in_2(in_18), .Addres(Addres_lw_sw), .Mask(mask_4_lw_sw), .Mask_2(mask_2_lw_sw));
  ALU_R alu_r_1 (
    .in_1(in_3), .in_3(A), .in_4(B), .in_5(in_18), .Output(mul___div), .low(Low_ALU), .hi(Hi_ALU));  // open: in_2
  Multiplexer #(.select(2), .width(4)) multiplexer_3 (
    .in0(mask_4_lw_sw), .in1(mask_4_push_pop), .out(Output_3), .sel(in_14));  // open: in2, in3, en
  // Probe on in_3
  Multiplexer #(.select(3), .width(32), .enable("false")) multiplexer_4 (
    .in0(Low_ALU), .in1(Low), .in2(Hi), .in3(out_I), .in4(kbd), .in5(in_11), .in6(Push_Pop), .out(Input),
    .sel(Selectores));  // open: in7
  KBD kbd_1 (.in_1(in_17), .in_2(in_24), .in_3(in_20), .Output(kbd), .KBD_Enable(KBD_Enable));
  Multiplexer #(.select(2), .width(2)) multiplexer_5 (
    .in0(mask_2_lw_sw), .in1(mask_2_push_pop), .out(Output_4), .sel(in_14));  // open: in2, in3, en
  Multiplexer #(.select(2), .width(5), .enable("false")) multiplexer_6 (
    .in0(in_12), .in1(in_8), .in2({5{1'b1}}), .out(sobreescribir), .sel(in_7));  // open: in3
  Hi_Low hi_low_1 (.in_2(Hi_ALU), .in_3(Low_ALU), .in_1(in_15), .Hi(Hi), .Low(Low), .in_4(in_1), .in_5(in_2));
  TTY tty_1 (.in_1(A), .out_2(out_29));
  Multiplexer #(.select(2), .width(32), .enable("false")) multiplexer_7 (
    .in0(B), .in1(A), .out(Ram_in), .sel(in_22));  // open: in2, in3
  Decoder #(.select(2)) decoder_2 (
    .out0(Output[0]), .out1(Output[1]), .out2(Output[2]), .out3(Output[3]), .sel(Output_2));  // open: en

  // Other names for the same wires on the sheet: Addres_Ram[15:0] = out_32; Const[15:0] = in_18;
  //   Destino[25:0] = in_23; EN_ALU_I = in_19; EN_ALU_R = in_13; EN_BC_PC = in_6; EN_escribir_Hi_Low = in_15;
  //   EN_KBD = in_24; EN_lw_sw = in_25; EN_RF = in_9; EN_TTY = in_21; Func_Code[5:0] = in_3; kbd_Available = in_17;
  //   kbd_Data[6:0] = in_20; mask_2_Ram[1:0] = Output_4; mask_4[3:0] = Output; mask_4_Ram[3:0] = Output_3;
  //   mul_div_ALU = mul___div; Op_Code[5:0] = in_26; mask_2[1:0] = Output_2; PC[19:2] = {out_30, Output_2};
  //   Addres[15:0] = out_30; Ram_out[31:0] = in_11; Rd[4:0] = in_12; reloj = in_1; reset = in_2; Rs[4:0] = in_5;
  //   Rt[4:0] = in_8; s_Address_Ram[1:0] = in_14; s_BC[1:0] = in_10; s_escribir_RF[1:0] = in_7;
  //   s_input_RF[2:0] = Selectores; s_push_pop = in_16; s_Ram_in[1:0] = in_22;
  //   SP[19:2] = {Addres_push_pop, mask_2_push_pop}; TTY_Data[6:0] = out_29

  // Notes on the sheet:
  //   S_Address_Ram 
  //   PC
  //   Instruction Decoder
  //   S_Address_SP 
  //   Enables
  //   registro SP
  //   Output
  //   S_Address_PC 
endmodule

module ALU_I (
  input  [5:0] in_1,
  input  in_2,
  input  [31:0] in_3,
  input  [15:0] in_4,
  input  [31:0] in_5,
  output [31:0] Output
);

  wire addi, andi, beq, bgtz, blez, bltz, bne, lw, ori, slti, sltiu, sw, xori;
  wire [3:0] priority_encoder_1_out;
  wire [31:0] r_addi, r_andi, r_ori, r_slti_ltiu, r_sltisltiu, r_xori, s_beq, s_bgtz, s_blez, s_bltz, s_bne,
       s_lw, s_sw;

  and and_1 (beq, ~in_1[0], ~in_1[1], in_1[2], ~in_1[3], ~in_1[4], ~in_1[5]);  // AND_Gate
  and and_2 (bne, in_1[0], ~in_1[1], in_1[2], ~in_1[3], ~in_1[4], ~in_1[5]);  // AND_Gate
  addi addi_1 (.Rs(in_3), .cons(in_4), .Output(r_addi));
  beq beq_1 (.Rt(in_5), .Rs(in_3), .in_3(in_4), .OUT(s_beq));
  and and_3 (blez, ~in_1[0], in_1[1], in_1[2], ~in_1[3], ~in_1[4], ~in_1[5]);  // AND_Gate
  and and_4 (bgtz, in_1[0], in_1[1], in_1[2], ~in_1[3], ~in_1[4], ~in_1[5]);  // AND_Gate
  andi___ori__xori andi_ori_xori_1 (.Rs(in_3), .cons(in_4), .Output(r_andi));
  bne bne_1 (.Rt(in_5), .Rs(in_3), .in_3(in_4), .OUT(s_bne));
  Priority_Encoder #(.select(4)) priority_encoder_1 (
    .in0(beq), .in1(bne), .in2(blez), .in3(bgtz), .in4(bltz), .in5(addi), .in6(slti), .in7(sltiu), .in8(lw),
    .in9(sw), .in10(andi), .in11(xori), .in12(ori), .out(priority_encoder_1_out));  // open: in13, in14, in15, gs, en_out, en_in
  // Probe on priority_encoder_1_out
  ori ori_1 (.Rs(in_3), .cons(in_4), .Output(r_ori));
  blez blez_1 (.Rs(in_3), .in_2(in_4), .OUT(s_blez));
  and and_5 (bltz, in_1[0], ~in_1[1], ~in_1[2], ~in_1[3], ~in_1[4], ~in_1[5]);  // AND_Gate
  and and_6 (addi, ~in_1[0], ~in_1[1], ~in_1[2], in_1[3], ~in_1[4], ~in_1[5]);  // AND_Gate
  xori xori_1 (.Rs(in_3), .cons(in_4), .Output(r_xori));
  and and_7 (slti, ~in_1[0], in_1[1], ~in_1[2], in_1[3], ~in_1[4], ~in_1[5]);  // AND_Gate
  and and_8 (sltiu, in_1[0], in_1[1], ~in_1[2], in_1[3], ~in_1[4], ~in_1[5]);  // AND_Gate
  bgtz bgtz_1 (.Rs(in_3), .in_2(in_4), .OUT(s_bgtz));
  and and_9 (lw, in_1[0], in_1[1], ~in_1[2], ~in_1[3], ~in_1[4], in_1[5]);  // AND_Gate
  and and_10 (sw, in_1[0], in_1[1], ~in_1[2], in_1[3], ~in_1[4], in_1[5]);  // AND_Gate
  slti___sltiu slti_sltiu_1 (.in_1(in_1[0]), .Rs(in_3), .\const (in_4), .Output(r_sltisltiu));
  bltz bltz_1 (.Rs(in_3), .in_2(in_4), .OUT(s_bltz));
  Multiplexer #(.select(4), .width(32)) multiplexer_1 (
    .in0(s_beq), .in1(s_bne), .in2(s_blez), .in3(s_bgtz), .in4(s_bltz), .in5(r_addi), .in6(r_slti_ltiu),
    .in7(r_slti_ltiu), .in8(s_lw), .in9(s_sw), .in10(r_andi), .in11(r_ori), .in12(r_xori), .out(Output),
    .sel(priority_encoder_1_out), .en(in_2));  // open: in13, in14, in15
  and and_11 (andi, ~in_1[0], ~in_1[1], in_1[2], in_1[3], ~in_1[4], ~in_1[5]);  // AND_Gate
  and and_12 (ori, in_1[0], ~in_1[1], in_1[2], in_1[3], ~in_1[4], ~in_1[5]);  // AND_Gate
  and and_13 (xori, ~in_1[0], in_1[1], in_1[2], in_1[3], ~in_1[4], ~in_1[5]);  // AND_Gate

  // Other names for the same wires on the sheet: Const[15:0] = in_4; EN = in_2; con_signo = in_1[0];
  //   Func_Code[5:0] = in_1; Rs[31:0] = in_3; Rt[31:0] = in_5

  // Notes on the sheet:
  //   beq
  //   bne
  //   blez
  //   bgtz
  //   Tipo I
  //   bltz
  //   addi
  //   slti
  //   sltiu
  //   lw
  //   sw
  //   andi
  //   ori
  //   xori
endmodule

module TTY (
  input  [31:0] in_1,
  output [6:0] out_2
);


  assign out_2 = in_1[6:0];

  // Other names for the same wires on the sheet: Rs[31:0] = in_1

  // Notes on the sheet:
  //   La entrada del enable la sustitui  por una constante para que  siempre devuelva algo 
endmodule

module Branch_Control (
  input  in_1,
  input  [31:0] in_2,
  input  [25:0] in_3,
  input  [1:0] in_4,
  input  [31:0] in_5,
  output [31:0] Output
);

  wire [31:0] adder_2_out, jump, PC___4;

  Adder #(.width(32)) adder_1 (.a(in_5), .b(32'h4), .out(PC___4));  // open: cin, cout
  j_BC j_bc_1 (.in_1(in_2), .in_2(in_3), .j(jump));
  Adder #(.width(32)) adder_2 (.a(in_2), .b(PC___4), .out(adder_2_out));  // open: cin, cout
  Multiplexer #(.select(2), .width(32)) multiplexer_1 (
    .in0(PC___4), .in1(jump), .in2(in_2), .in3(adder_2_out), .out(Output), .sel(in_4), .en(in_1));

  // Other names for the same wires on the sheet: destino[25:0] = in_3; EN = in_1; PC[31:0] = in_5;
  //   registro[31:0] = in_2; selector[1:0] = in_4
endmodule

module j_BC (
  input  [31:0] in_1,
  input  [25:0] in_2,
  output [31:0] j
);


  assign j = {in_1[31:28], in_2, 2'b00};

  // Other names for the same wires on the sheet: destino[25:0] = in_2; PC[31:0] = in_1
endmodule

module Hi_Low (
  input  in_1,
  input  [31:0] in_2,
  input  [31:0] in_3,
  input  in_4,
  input  in_5,
  output [31:0] Hi,
  output [31:0] Low
);

  Register #(.width(32)) register_1 (.D(in_3), .en(in_1), .Q(Low), .clk(in_4), .clr(in_5));
  Register #(.width(32)) register_2 (.D(in_2), .en(in_1), .Q(Hi), .clk(in_4), .clr(in_5));

  // Other names for the same wires on the sheet: escribir = in_1; Hi_t[31:0] = in_2; Low_t[31:0] = in_3;
  //   readed_Hi[31:0] = Hi; readed_Low[31:0] = Low; reloj = in_4; reset = in_5

  // Notes on the sheet:
  //   El hi y el low siempre estan actualizados
endmodule

module Control_Unit (
  input  [31:0] in_1,
  input  in_2,
  input  in_3,
  input  [3:0] in_4,
  input  [3:0] in_5,
  input  in_6,
  output [5:0] out_7,
  output [2:0] selectores,
  output out_9,
  output [4:0] out_10,
  output [1:0] out_11,
  output out_12,
  output out_13,
  output out_14,
  output [4:0] out_15,
  output [1:0] out_16,
  output out_17,
  output out_18,
  output out_19,
  output [4:0] out_20,
  output [1:0] out_21,
  output out_22,
  output out_23,
  output out_24,
  output [15:0] out_25,
  output out_26,
  output out_27,
  output [1:0] out_28,
  output out_29,
  output out_30,
  output out_31,
  output [25:0] out_32,
  output out_33,
  output out_34,
  output out_35,
  output out_36,
  output [5:0] out_37
);

  wire a, and_1_out, cs_1, cs_2, cs_3, cs_4, d_ff_5_q, d_ff_7_q, d_ff_10_q, d_ff_12_q, d_ff_13_q, d_ff_15_q,
       d_ff_16_q, demultiplexer_1_out0, demultiplexer_6_out1, demultiplexer_9_out1, e_write_RF_1,
       e_write_RF_2, e_write_RF_3, e_write_RF_4, e_write_RF_6, e_write_RF_7, e_write_RF_8, e_write_RF_9,
       EN_ALU_I_2, EN_ALU_R_1, En_BC_PC_1, En_BC_PC_2, EN_ciclo_2, EN_ciclo_3, EN_ciclo_5, EN_Inst_Mem_1,
       EN_Inst_Mem_2, EN_Inst_Mem_esp_1, EN_Inst_Mem_esp_4, EN_Inst_Mem_esp_5, EN_Inst_Mem_esp_6, fin_ciclo,
       halt, halt_EN, I_J, I_Ram, I_RF, I_RF_EN_1, J, J_EN, kbd, leer_escribir_Ram, lw_sw, nop, nop_EN,
       nor_1_out, or_1_out, or_2_out, or_3_out, or_4_out, or_6_out, or_8_out, or_13_out, or_15_out,
       or_30_out, P, P_EN, push_pop, R_ALU_1, R_jr, R_jr_EN, R_mflo___mfhi, R_mflo___mfhi_1, R_RF, rnd,
       s_Address_Lw_Sw, s_Address_Push_Pop, s_Input_RF_ALU, s_Input_RF_Hi, s_Input_RF_Low,
       s_Input_RF_Push_Pop, s_Input_RF_Ram_out, s_write_RF_d, s_write_RF_SP, s_write_RF_t, tty, xnor_1_out;
  wire [3:0] counter_1_q, selec_operaciones, Time;

  or or_1 (or_1_out, EN_Inst_Mem_2, EN_ciclo_5);
  Demultiplexer #(.enable("false")) demultiplexer_1 (
    .out0(demultiplexer_1_out0), .out1(EN_ciclo_2), .in(out_23), .sel(out_37[3]));
  Demultiplexer #(.enable("false")) demultiplexer_2 (.out0(EN_ciclo_3), .out1(e_write_RF_9), .in(P_EN), .sel(out_7[0]));
  Demultiplexer #(.enable("false")) demultiplexer_3 (
    .out0(EN_Inst_Mem_2), .out1(EN_Inst_Mem_1), .in(out_27), .sel(fin_ciclo));
  D_Flip_Flop #(.trigger("falling")) d_ff_1 (
    .clk(in_2), .D(or_1_out), .Q(out_27), .preset(in_3));  // open: Qn, en, reset
  Demultiplexer #(.enable("false")) demultiplexer_4 (.out0(e_write_RF_1), .out1(out_26), .in(EN_ALU_R_1), .sel(in_6));
  D_Flip_Flop #(.trigger("falling")) d_ff_2 (
    .clk(in_2), .D(e_write_RF_3), .Q(I_RF_EN_1), .reset(in_3));  // open: Qn, preset, en
  or or_2 (or_2_out, cs_1, demultiplexer_1_out0);
  or or_3 (or_3_out, cs_2, EN_ciclo_2);
  or or_4 (or_4_out, cs_3, EN_ciclo_3);
  or or_5 (s_Address_Push_Pop, P_EN, cs_4, cs_3);
  D_Flip_Flop #(.trigger("falling")) d_ff_3 (
    .clk(in_2), .D(EN_Inst_Mem_1), .Q(out_29), .reset(in_3));  // open: Qn, preset, en
  // Probe on selec_operaciones
  or or_6 (or_6_out, out_9, halt_EN);
  Demultiplexer #(.enable("false")) demultiplexer_5 (
    .out0(cs_1), .out1(EN_Inst_Mem_esp_4), .in(EN_Inst_Mem_esp_1), .sel(fin_ciclo));
  D_Flip_Flop #(.trigger("falling")) d_ff_4 (
    .clk(in_2), .D(or_2_out), .Q(EN_Inst_Mem_esp_1), .reset(in_3));  // open: Qn, preset, en
  D_Flip_Flop #(.trigger("falling")) d_ff_5 (
    .clk(in_2), .D(or_3_out), .Q(d_ff_5_q), .reset(in_3));  // open: Qn, preset, en
  Demultiplexer #(.enable("false")) demultiplexer_6 (
    .out0(cs_2), .out1(demultiplexer_6_out1), .in(d_ff_5_q), .sel(fin_ciclo));
  Demultiplexer #(.enable("false")) demultiplexer_7 (
    .out0(cs_3), .out1(EN_Inst_Mem_esp_6), .in(EN_Inst_Mem_esp_5), .sel(fin_ciclo));
  D_Flip_Flop #(.trigger("falling")) d_ff_6 (
    .clk(in_2), .D(or_4_out), .Q(EN_Inst_Mem_esp_5), .reset(in_3));  // open: Qn, preset, en
  D_Flip_Flop #(.trigger("falling")) d_ff_7 (
    .clk(in_2), .D(out_29), .Q(d_ff_7_q), .reset(in_3));  // open: Qn, preset, en
  Demultiplexer #(.select(4), .enable("false")) demultiplexer_8 (
    .out0(EN_ALU_R_1), .out1(R_jr_EN), .out2(e_write_RF_3), .out3(EN_ALU_I_2), .out4(J_EN), .out5(P_EN),
    .out6(nop_EN), .out7(e_write_RF_2), .out8(out_23), .out9(halt_EN), .out10(out_22), .out11(e_write_RF_4),
    .out12(out_36), .in(d_ff_7_q), .sel(selec_operaciones));  // open: out13, out14, out15
  D_Flip_Flop #(.trigger("falling")) d_ff_8 (
    .clk(in_2), .D(or_6_out), .Q(out_9), .reset(in_3));  // open: Qn, preset, en
  Instruction_Decoder instruction_decoder_1 (
    .in_1(in_1), .Rt(out_15), .Constante(out_25), .Func_Code(out_7), .Rd(out_20), .Rs(out_10),
    .Destino_salto(out_32), .out_13(J), .out_16(P), .out_14(halt), .Op_Code(out_37), .out_12(I_RF),
    .out_19(I_J), .out_17(R_jr), .out_20(nop), .out_18(I_Ram), .out_21(tty), .out_15(rnd), .out_22(kbd),
    .out_10(R_RF), .out_11(R_mflo___mfhi));  // open: x
  or or_7 (R_ALU_1, e_write_RF_1, out_26);
  D_Flip_Flop #(.trigger("falling")) d_ff_9 (
    .clk(in_2), .D(EN_Inst_Mem_esp_4), .Q(e_write_RF_6), .reset(in_3));  // open: Qn, preset, en
  D_Flip_Flop #(.trigger("falling")) d_ff_10 (
    .clk(in_2), .D(demultiplexer_6_out1), .Q(d_ff_10_q), .reset(in_3));  // open: Qn, preset, en
  D_Flip_Flop #(.trigger("falling")) d_ff_11 (
    .clk(in_2), .D(EN_Inst_Mem_esp_6), .Q(e_write_RF_7), .reset(in_3));  // open: Qn, preset, en
  or or_8 (or_8_out, cs_4, e_write_RF_9);
  D_Flip_Flop #(.trigger("falling")) d_ff_12 (
    .clk(in_2), .D(e_write_RF_6), .Q(d_ff_12_q), .reset(in_3));  // open: Qn, preset, en
  Demultiplexer #(.enable("false")) demultiplexer_9 (
    .out0(cs_4), .out1(demultiplexer_9_out1), .in(d_ff_13_q), .sel(fin_ciclo));
  D_Flip_Flop #(.trigger("falling")) d_ff_13 (
    .clk(in_2), .D(or_8_out), .Q(d_ff_13_q), .reset(in_3));  // open: Qn, preset, en
  or or_9 (lw_sw, d_ff_12_q, d_ff_10_q);
  D_Flip_Flop #(.trigger("falling")) d_ff_14 (
    .clk(in_2), .D(e_write_RF_7), .Q(e_write_RF_8), .reset(in_3));  // open: Qn, preset, en
  Demultiplexer #(.enable("false")) demultiplexer_10 (
    .out0(s_Input_RF_Hi), .out1(s_Input_RF_Low), .in(e_write_RF_2), .sel(out_7[1]));
  D_Flip_Flop #(.trigger("falling")) d_ff_15 (
    .clk(in_2), .D(demultiplexer_9_out1), .Q(d_ff_15_q), .reset(in_3));  // open: Qn, preset, en
  or or_10 (En_BC_PC_1, nop_EN, R_ALU_1, lw_sw, R_mflo___mfhi_1, push_pop, I_RF_EN_1, out_22, e_write_RF_4, out_36);
  or or_11 (En_BC_PC_2, EN_ALU_I_2, J_EN, R_jr_EN);
  or or_12 (R_mflo___mfhi_1, s_Input_RF_Hi, s_Input_RF_Low);
  or or_13 (or_13_out, En_BC_PC_1, En_BC_PC_2);
  Multiplexer #(.width(4)) multiplexer_1 (.in0(in_4), .in1(in_5), .out(Time), .sel(out_17));  // open: en
  D_Flip_Flop #(.trigger("falling")) d_ff_16 (
    .clk(in_2), .D(e_write_RF_8), .Q(d_ff_16_q), .reset(in_3));  // open: Qn, preset, en
  Priority_Encoder #(.select(4)) priority_encoder_1 (
    .in0(R_RF), .in1(R_jr), .in2(I_RF), .in3(I_J), .in4(J), .in5(P), .in6(nop), .in7(R_mflo___mfhi),
    .in8(I_Ram), .in9(halt), .in10(tty), .in11(rnd), .in12(kbd), .out(selec_operaciones));  // open: in13, in14, in15, gs, en_out, en_in
  xnor xnor_1 (xnor_1_out, a, nor_1_out);
  or or_14 (push_pop, d_ff_16_q, d_ff_15_q);
  and and_1 (and_1_out, or_13_out, ~out_9);  // AND_Gate
  or or_15 (or_15_out, ~xnor_1_out, out_12);  // OR_Gate
  D_Flip_Flop #(.trigger("falling")) d_ff_17 (
    .clk(in_2), .D(and_1_out), .Q(EN_ciclo_5), .reset(in_3));  // open: Qn, preset, en
  D_Flip_Flop #(.trigger("falling")) d_ff_18 (.clk(in_2), .D(or_15_out), .Q(a), .reset(in_3));  // open: Qn, preset, en
  Counter #(.width(4), .max('hf)) counter_1 (
    .load(or_15_out), .D(Time), .count(a), .Q(counter_1_q), .clk(in_2), .clr(in_3));  // open: carry
  nor nor_1 (nor_1_out, counter_1_q[0], counter_1_q[1], counter_1_q[2], counter_1_q[3]);
  or or_16 (out_12, cs_1, cs_2, out_27, cs_3, cs_4);
  and and_2 (fin_ciclo, nor_1_out, a);
  or or_17 (out_13, En_BC_PC_2, En_BC_PC_1);
  or or_18 (out_31, EN_Inst_Mem_1, EN_Inst_Mem_2, out_27);
  or or_19 (s_write_RF_d, e_write_RF_1, R_mflo___mfhi_1, e_write_RF_7, e_write_RF_4, out_36);
  or or_20 (s_write_RF_t, e_write_RF_3, e_write_RF_6);
  or or_21 (out_19, e_write_RF_1, e_write_RF_2, e_write_RF_3, e_write_RF_4, e_write_RF_9, out_36, e_write_RF_6, e_write_RF_7, e_write_RF_8);
  Priority_Encoder #(.select(2)) priority_encoder_2 (
    .in0(En_BC_PC_1), .in1(J_EN), .in2(R_jr_EN), .in3(EN_ALU_I_2), .out(out_11));  // open: gs, en_out, en_in
  or or_22 (s_write_RF_SP, e_write_RF_8, e_write_RF_9);
  or or_23 (s_Input_RF_ALU, e_write_RF_1, e_write_RF_4);
  or or_24 (out_18, e_write_RF_3, EN_ALU_I_2);
  Priority_Encoder #(.select(2)) priority_encoder_3 (
    .in0(s_write_RF_d), .in1(s_write_RF_t), .in2(s_write_RF_SP), .out(out_16));  // open: in3, gs, en_out, en_in
  or or_25 (s_Address_Lw_Sw, out_23, cs_1, cs_2);
  or or_26 (s_Input_RF_Ram_out, e_write_RF_6, e_write_RF_7);
  or or_27 (s_Input_RF_Push_Pop, e_write_RF_8, e_write_RF_9);
  or or_28 (out_14, EN_ALU_R_1, e_write_RF_4);
  Priority_Encoder #(.select(2)) priority_encoder_4 (
    .in0(s_Address_Lw_Sw), .in1(s_Address_Push_Pop), .out(out_21));  // open: in2, in3, gs, en_out, en_in
  or or_29 (leer_escribir_Ram, out_23, EN_Inst_Mem_2);
  or or_30 (or_30_out, cs_1, cs_3, EN_Inst_Mem_2);
  Priority_Encoder #(.select(2)) priority_encoder_5 (
    .in0(EN_ciclo_2), .in1(e_write_RF_9), .out(out_28));  // open: in2, in3, gs, en_out, en_in
  or or_31 (out_34, EN_ciclo_2, e_write_RF_9);
  not not_1 (out_17, or_30_out);
  or or_32 (out_35, EN_Inst_Mem_esp_1, cs_1, cs_3, EN_Inst_Mem_esp_4, EN_Inst_Mem_esp_5, EN_Inst_Mem_esp_6);
  Priority_Encoder priority_encoder_6 (
    .in0(s_Input_RF_ALU), .in1(s_Input_RF_Low), .in2(s_Input_RF_Hi), .in3(e_write_RF_3), .in4(out_36),
    .in5(s_Input_RF_Ram_out), .in6(s_Input_RF_Push_Pop), .out(selectores));  // open: in7, en_in, gs, en_out

  assign out_24 = out_7[0];
  assign out_33 = out_22;

  // Other names for the same wires on the sheet: Const[15:0] = out_25; cs = out_12; Destino[25:0] = out_32;
  //   e_halt = out_9; EN_read_Hi_Low = e_write_RF_2; R_mflo___mfhi_EN = e_write_RF_2; EN_ALU_I = out_18;
  //   EN_ALU_R = out_14; En_BC_PC = out_13; END = EN_ciclo_5; EN_Inst_Mem = out_31; EN_Inst_Mem_esp = out_35;
  //   EN_Push_Pop = out_30; EN_read_RF = out_29; EN_Smips_Escribir = out_34; EN_write_Hi_Low = out_26;
  //   EN_write_RF = out_19; Func_Code[5:0] = out_7; s_push_pop = out_7[0]; Input[31:0] = in_1;
  //   leer_escribir_Ram_3 = EN_Inst_Mem_2; nRead_Write_3 = EN_Inst_Mem_2; mul_div_ALU = in_6; nRead_Write = out_17;
  //   Op_Code[5:0] = out_37; R_ALU_En = EN_ALU_R_1; Rd[4:0] = out_20; cs_5 = out_27; EN_Inst_Mem_3 = out_27;
  //   read_inicio = out_27; Read_Time[3:0] = in_4; reloj = in_2; reset = in_3; Rs[4:0] = out_10; Rt[4:0] = out_15;
  //   s_Address[1:0] = out_21; e_low_sw = out_23; I_Ram_EN = out_23; leer_escribir_Ram_1 = out_23;
  //   s_Address_Lw_Sw_1 = out_23; EN_Inst_Mem_esp_2 = cs_1; nRead_Write_4 = cs_1; s_Address_Lw_Sw_2 = cs_1;
  //   s_Address_Lw_Sw_3 = cs_2; s_Address_Push_Pop_1 = P_EN; s_Address_Push_Pop_2 = cs_4; EN_Inst_Mem_esp_3 = cs_3;
  //   nRead_Write_1 = cs_3; s_Address_Push_Pop_3 = cs_3; s_BC[1:0] = out_11; R_jr_EN_1 = R_jr_EN; s_BC_A = R_jr_EN;
  //   J_EN_1 = J_EN; s_BC_jump = J_EN; I_J_EN = EN_ALU_I_2; I_J_EN_1 = EN_ALU_I_2; s_BC_out_I = EN_ALU_I_2;
  //   s_BC_PC_4 = En_BC_PC_1; s_Input_RF[2:0] = selectores; s_Ram_In[1:0] = out_28; EN_Smips_Escribir_1 = EN_ciclo_2;
  //   s_Ram_In_Sw = EN_ciclo_2; s_write_RF[1:0] = out_16; s_Input_RF_ALU_1 = e_write_RF_1;
  //   s_write_RF_d_1 = e_write_RF_1; s_write_RF_d_2 = R_mflo___mfhi_1; s_Input_RF_Ram_out_2 = e_write_RF_7;
  //   s_write_RF_d_3 = e_write_RF_7; EN_ALU_R_2 = e_write_RF_4; rnd_EN = e_write_RF_4; rnd_EN_1 = e_write_RF_4;
  //   s_Input_RF_ALU_2 = e_write_RF_4; s_write_RF_d_4 = e_write_RF_4; e_kbd = out_36; e_write_RF_5 = out_36;
  //   kbd_EN = out_36; kbd_EN_1 = out_36; s_Input_RF_kbd = out_36; s_write_RF_d_5 = out_36;
  //   s_Input_RF_Push_Pop_1 = e_write_RF_8; s_write_RF_SP_1 = e_write_RF_8; EN_Smips_Escribir_2 = e_write_RF_9;
  //   s_Input_RF_Push_Pop_2 = e_write_RF_9; s_Ram_In_Push = e_write_RF_9; s_write_RF_SP_2 = e_write_RF_9;
  //   EN_ALU_I_1 = e_write_RF_3; I_RF_EN = e_write_RF_3; s_Input_RF_out_I = e_write_RF_3;
  //   s_write_RF_t_1 = e_write_RF_3; s_Input_RF_Ram_out_1 = e_write_RF_6; s_write_RF_t_2 = e_write_RF_6;
  //   tty_EN = out_22; tty_EN_1 = out_22; TTY_Enable = out_22; Write_Time[3:0] = in_5

  // Notes on the sheet:
  //   I-RF
  //   I-BC
  //   Lw-Sw
  //   Push-Pop
  //   pop
  //   push
  //   Esta flag me la da la ALU y me dice si fue una mult o una div
  //   R-ALU
  //   lw
  //   sw
  //   Instrucciones especiales
  //   Halt
  //   Jump
  //   TTY
  //   Enables
  //   KBD
  //   R-jr
  //   R- mflo/ mfhi
  //   RND
  //   Instruction Decoder
  //   Ciclo
  //   En_CS
  //   En_BC-PC
  //   En_Instruction_Memory
  //   En_Write_RF
  //   Select registro donde se va a escribir en el RF
  //   select_BC
  //   S_Input_RF
  //   En_ALU_I
  //   s_push_pop
  //   S_Address_Lw_Sw
  //   En Push_Pop
  //   En_ALU_R
  //   S_Address
  //   Leer_Escribir_Ram
  //   !Read / Write Ram
  //   S_Ram_In
  //   En_Inst_Mem_especial
  //   En-Inst_Mem_Escribir_Smips
endmodule

module KBD (
  input  in_1,
  input  in_2,
  input  [6:0] in_3,
  output [31:0] Output,
  output KBD_Enable
);

  Multiplexer #(.width(32)) multiplexer_1 (
    .in0({{25{1'b0}}, in_3}), .in1({32{1'b1}}), .out(Output), .sel(in_1), .en(in_2));
  and and_1 (KBD_Enable, in_2, in_1);

  // Other names for the same wires on the sheet: kbd_Data[6:0] = in_3; EN = in_2; kbd_Available = in_1

  // Notes on the sheet:
  //   Pendiente el kbd_clear
endmodule

module Inversor (
  input  [31:0] in_1,
  output [31:0] Output
);


  assign Output = {in_1[7:0], in_1[15:8], in_1[23:16], in_1[31:24]};

  // Other names for the same wires on the sheet: _3[7:0] = in_1[31:24]; Input[31:0] = in_1; _2[7:0] = in_1[23:16];
  //   _1[7:0] = in_1[15:8]; _0[7:0] = in_1[7:0]
endmodule

module precaucion (
  input  in_1,
  input  in_2,
  output [31:0] Output
);

  wire and_1_out, and_2_out, CU_EN_PC, d_ff_2_q, d_ff_3_q, demultiplexer_1_out0, demultiplexer_1_out1,
       demultiplexer_2_out0, EN, END, leer_escibir_Ram, leer_inicio, nop_EN, nop_EN_1, not_1_out, or_1_out,
       or_2_out, reloj, reset, s_Address_Ram, s_PC, s_simple_BC, s_simple_BC_1, salto_regular;
  wire [1:0] mask_2, mask_2_lw_sw, mask_2_PC_PC, mask_2_push_pop, mask_2_Ram, priority_encoder_1_out,
       s_Addres, s_Address_Ram_1;
  wire [3:0] mask_4, mask_4_lw_sw, mask_4_PC_PC, mask_4_push_pop, mask_4_Ram;
  wire [15:0] Addres, Addres_lw_sw, Addres_push_pop, Addres_Ram, Address_PC;
  wire [31:0] A, BC, Input, Input_1, jump, multiplexer_1_out, PC, PC___4, Ram_out, salto_irregular;

  Multiplexer #(.width(32), .enable("false")) multiplexer_1 (.in0(BC), .in1(A), .out(multiplexer_1_out), .sel(s_PC));
  Register #(.width(32)) register_1 (
    .D(multiplexer_1_out), .en(CU_EN_PC), .Q({PC[31:20], Addres, mask_2, PC[1:0]}), .clk(reloj));  // open: clr
  Multiplexer #(.width(16)) multiplexer_2 (
    .in0(Addres_lw_sw), .in1(Addres_push_pop), .out(Addres_Ram), .sel(s_Address_Ram));  // open: en
  Multiplexer #(.width(16)) multiplexer_3 (
    .in0(Address_PC), .in1(Addres_Ram), .out(Addres), .sel(leer_escibir_Ram));  // open: en
  Multiplexer #(.select(2), .width(16)) multiplexer_4 (
    .in0(Address_PC), .in1(Addres_lw_sw), .in2(Addres_push_pop), .out(Addres), .sel(s_Addres));  // open: in3, en
  and and_1 (and_1_out, in_1, ~in_2);  // AND_Gate
  and and_2 (and_2_out, ~in_1, in_2);  // AND_Gate
  D_Flip_Flop #(.trigger("falling")) d_ff_1 (
    .clk(reloj), .D(nop_EN), .Q(nop_EN_1), .reset(reset));  // open: Qn, preset, en
  // Probe on mask_4
  Multiplexer #(.width(4)) multiplexer_5 (
    .in0(mask_4_PC_PC), .in1(mask_4_Ram), .out(mask_4), .sel(leer_escibir_Ram));  // open: en
  Multiplexer #(.select(2), .width(16)) multiplexer_6 (
    .in0(Addres_lw_sw), .in1(Addres_push_pop), .in2(Address_PC), .out(Addres), .sel(s_Address_Ram_1));  // open: in3, en
  nor nor_1 (salto_regular, in_1, in_2);
  Multiplexer #(.width(4)) multiplexer_7 (
    .in0(mask_4_lw_sw), .in1(mask_4_push_pop), .out(mask_4_Ram), .sel(s_Address_Ram));  // open: en
  Priority_Encoder #(.select(2)) priority_encoder_1 (
    .in0(salto_regular), .in1(and_1_out), .in2(and_2_out), .out(priority_encoder_1_out));  // open: in3, gs, en_out, en_in
  Multiplexer #(.select(2), .width(4)) multiplexer_8 (
    .in0(mask_4_PC_PC), .in2(mask_4_lw_sw), .in3(mask_4_push_pop), .out(mask_4), .sel(s_Addres));  // open: in1, en
  // Probe on priority_encoder_1_out
  or or_1 (or_1_out, demultiplexer_1_out0, END);
  Multiplexer #(.width(2)) multiplexer_9 (
    .in0(mask_2_PC_PC), .in1(mask_2_Ram), .out(mask_2), .sel(leer_escibir_Ram));  // open: en
  Multiplexer #(.width(16)) multiplexer_10 (
    .in0(Addres_lw_sw), .in1(Addres_push_pop), .out(Addres_Ram), .sel(s_Address_Ram));  // open: en
  Multiplexer #(.width(16)) multiplexer_11 (
    .in0(Addres_Ram), .in1(Address_PC), .out(Addres), .sel(leer_escibir_Ram));  // open: en
  Multiplexer #(.select(2), .width(4)) multiplexer_12 (
    .in0(mask_4_lw_sw), .in1(mask_4_push_pop), .in2(mask_4_PC_PC), .out(mask_4), .sel(s_Address_Ram_1));  // open: in3, en
  Multiplexer #(.select(2), .width(32)) multiplexer_13 (
    .in0(PC___4), .in1(jump), .in2(salto_irregular), .out(Output), .sel(priority_encoder_1_out), .en(EN));  // open: in3
  D_Flip_Flop #(.trigger("falling")) d_ff_2 (
    .clk(reloj), .D(or_1_out), .Q(d_ff_2_q), .reset(reset));  // open: Qn, preset, en
  Demultiplexer #(.enable("false")) demultiplexer_1 (
    .out0(demultiplexer_1_out0), .out1(demultiplexer_1_out1), .in(d_ff_2_q), .sel(not_1_out));
  Multiplexer #(.width(2)) multiplexer_14 (
    .in0(mask_2_lw_sw), .in1(mask_2_push_pop), .out(mask_2_Ram), .sel(s_Address_Ram));  // open: en
  not not_1 (not_1_out, reset);
  // Probe on mask_4
  Multiplexer #(.width(4)) multiplexer_15 (
    .in0(mask_4_Ram), .in1(mask_4_PC_PC), .out(mask_4), .sel(leer_escibir_Ram));  // open: en
  Multiplexer #(.select(2), .width(2)) multiplexer_16 (
    .in0(mask_2_PC_PC), .in2(mask_2_lw_sw), .in3(mask_2_push_pop), .out(mask_2), .sel(s_Addres));  // open: in1, en
  Multiplexer #(.width(4)) multiplexer_17 (
    .in0(mask_4_lw_sw), .in1(mask_4_push_pop), .out(mask_4_Ram), .sel(s_Address_Ram));  // open: en
  D_Flip_Flop #(.trigger("falling")) d_ff_3 (
    .clk(reloj), .D(or_2_out), .Q(d_ff_3_q), .reset(reset));  // open: Qn, preset, en
  or or_2 (or_2_out, demultiplexer_2_out0, END);
  Multiplexer #(.select(2), .width(2)) multiplexer_18 (
    .in0(mask_2_lw_sw), .in1(mask_2_push_pop), .in2(mask_2_PC_PC), .out(mask_2), .sel(s_Address_Ram_1));  // open: in3, en
  Demultiplexer #(.enable("false")) demultiplexer_2 (
    .out0(demultiplexer_2_out0), .in(d_ff_3_q), .sel(reset));  // open: out1
  Decoder #(.select(2)) decoder_1 (
    .out0(mask_4[0]), .out1(mask_4[1]), .out2(mask_4[2]), .out3(mask_4[3]), .sel(mask_2));  // open: en
  Multiplexer #(.width(2)) multiplexer_19 (
    .in0(mask_2_Ram), .in1(mask_2_PC_PC), .out(mask_2), .sel(leer_escibir_Ram));  // open: en
  Multiplexer #(.width(2)) multiplexer_20 (
    .in0(mask_2_lw_sw), .in1(mask_2_push_pop), .out(mask_2_Ram), .sel(s_Address_Ram));  // open: en
  Multiplexer #(.width(32), .enable("false")) multiplexer_21 (
    .in0(Input_1), .in1(Ram_out), .out(Input), .sel(leer_inicio));
  or or_3 (s_simple_BC, s_simple_BC_1, s_simple_BC_1);
  buf or_4 (s_simple_BC, s_simple_BC_1);  // OR_Gate

  // Other names for the same wires on the sheet: es_salto = in_1; es_salto_irregular = in_2;
  //   PC[19:2] = {Addres, mask_2}

  // Notes on the sheet:
  //   BC
  //   PC
  //   S_Address_Ram 
  //   Lectura de la Ram
  //   Nop
  //   S_Address_Ram 
  //   es_salto y es_salto_irregular no pueden ser 1 simultaneamente
  //   S_Address_Ram 
  //   Lectura de la Ram
  //   Inicio del Control Unit
  //   S_Address_PC 
endmodule

module Push_Pop (
  input  [31:0] in_1,
  input  in_2,
  output [31:0] Output,
  output [3:0] Mask,
  output [1:0] Mask_2,
  output [15:0] Addres
);

  wire [31:0] adder_1_out, subtractor_1_out;

  Adder #(.width(32)) adder_1 (.a(in_1), .b(32'h4), .out(adder_1_out));  // open: cin, cout
  Multiplexer #(.width(32)) multiplexer_1 (
    .in0(adder_1_out), .in1(subtractor_1_out), .out(Output), .sel(in_2));  // open: en
  Subtractor #(.width(32)) subtractor_1 (.a(in_1), .b(32'h4), .out(subtractor_1_out));  // open: bin, bout
  Decoder #(.select(2)) decoder_1 (
    .out0(Mask[0]), .out1(Mask[1]), .out2(Mask[2]), .out3(Mask[3]), .sel(in_1[3:2]));  // open: en

  assign Addres = in_1[19:4];
  assign Mask_2 = in_1[1:0];

  // Other names for the same wires on the sheet: s_push_pop = in_2; SP[31:0] = in_1
endmodule
